// Logisim project Computer-v2.circ as structural Verilog: 14 circuits, main circuit Main
module Main (
);

  wire and_1_out, and_2_out, clock_1_out, controlled_buffer_1_out, controlled_buffer_13_out,
       datatypedecoder_1_iq1ad, datatypedecoder_1_iq1out, datatypedecoder_1_iq2ad, datatypedecoder_1_iq2out,
       decoder_1_out0, iqctrl_1_stop, not_1_out, not_2_out, not_3_out, not_5_out, or_1_out, or_2_out,
       or_3_out, or_4_out, or_5_out, or_6_out, ram_1_p4, register_1_q, Reset_out, undriven, undriven_3;
  wire [1:0] extraregistercontroller_1_er0_we_oe, extraregistercontroller_1_er1_we_oe,
       extraregistercontroller_1_er2_we_oe, extraregistercontroller_1_er3_we_oe,
       extraregistercontroller_1_er4_we_oe, extraregistercontroller_1_er5_we_oe,
       extraregistercontroller_1_er6_we_oe, extraregistercontroller_1_er7_we_oe,
       queuesizedecoder_1_queuesize, typedecoderunit_1_datatype;
  wire [2:0] instructiontypedecoder_1_alu, instructiontypedecoder_1_cj, instructiontypedecoder_1_erc,
       instructiontypedecoder_1_rc1, instructiontypedecoder_1_rc2;
  wire [3:0] iqctrl_1_state, typedecoderunit_1_instructiontype;
  wire [4:0] alu_1_flagout, and_4_out, decoder_1_out1, Flag_q;
  wire [7:0] undriven_2;
  wire [15:0] AddressBus, alu_1_divremainder, alu_1_output, controlled_buffer_2_out, counter_1_q, DataBus,
       DivOut_q, EEPROM_data, Instruction_q, IQ1Addr_out, IQ1Data_out, IQ2Addr_out, IQ2Data_out,
       portunit_1_portc_out, Queue1_q, Queue2_q, ram_1_p1, ram_1_p5, RegA_q, RegB_q, register_2_q,
       register_3_q, screencontroller_1_d, screencontroller_1_d_1, screencontroller_1_d_2,
       screencontroller_1_d_3, screencontroller_1_d_4, screencontroller_1_d_5, screencontroller_1_d_6,
       screencontroller_1_d_7, screencontroller_1_d_8, screencontroller_1_d_9, screencontroller_1_d_10,
       screencontroller_1_d_11, screencontroller_1_d_12, screencontroller_1_d_13, screencontroller_1_d_14,
       screencontroller_1_d_15, screencontroller_1_d_16, screencontroller_1_d_17, screencontroller_1_d_18,
       screencontroller_1_d_19, screencontroller_1_d_20, screencontroller_1_d_21, screencontroller_1_d_22,
       screencontroller_1_d_23, screencontroller_1_dataout, undriven_4;
  wire [31:0] CS1;

  ROM #(.addrWidth(16), .dataWidth(16)) EEPROM (.addr(controlled_buffer_2_out), .data(EEPROM_data));
  // RAM #(.addrWidth(16), .dataWidth(16), .databus("bidir"), .enables("line"), .trigger("falling")) ram_1: pin names not known; wires that end beside it: ram_1_p1, CS1[14], CS1[13], ram_1_p4, ram_1_p5
  not not_1 (not_1_out, and_1_out);
  Register #(.trigger("falling"), .width(16)) Instruction (
    .D(DataBus), .en(iqctrl_1_state[0]), .Q(Instruction_q), .clk(ram_1_p4), .clr(Reset_out));
  Register #(.trigger("falling"), .width(16)) Queue1 (
    .D(DataBus), .en(iqctrl_1_state[1]), .Q(Queue1_q), .clk(ram_1_p4), .clr(Reset_out));
  Register #(.trigger("falling"), .width(16)) Queue2 (
    .D(DataBus), .en(iqctrl_1_state[2]), .Q(Queue2_q), .clk(ram_1_p4), .clr(Reset_out));
  TypeDecoderUnit typedecoderunit_1 (
    .Instruction(Instruction_q[5:0]), .DataType(typedecoderunit_1_datatype),
    .InstructionType(typedecoderunit_1_instructiontype));
  CentralUnit centralunit_1 (.Instruction(Instruction_q[5:0]), .OE(and_2_out), .ControlSignal(CS1));
  assign controlled_buffer_1_out = and_1_out ? not_1_out : 1'bz;  // Controlled_Buffer controlled_buffer_1
  or or_1 (or_1_out, CS1[21], controlled_buffer_1_out);
  assign controlled_buffer_2_out = or_1_out ? AddressBus : 16'bz;  // Controlled_Buffer controlled_buffer_2
  assign DataBus = or_2_out ? EEPROM_data : 16'bz;  // Controlled_Buffer controlled_buffer_3
  or or_2 (or_2_out, controlled_buffer_1_out, CS1[21]);
  assign ram_1_p5 = CS1[13] ? DataBus : 16'bz;  // Controlled_Buffer controlled_buffer_4
  QueueSizeDecoder queuesizedecoder_1 (.DataType(typedecoderunit_1_datatype), .QueueSize(queuesizedecoder_1_queuesize));
  assign DataBus = CS1[18] ? counter_1_q : 16'bz;  // Controlled_Buffer controlled_buffer_5
  Counter #(.max('hffff), .trigger("falling"), .width(16)) counter_1 (
    .load(and_1_out), .D(DataBus), .count(controlled_buffer_1_out), .Q(counter_1_q), .clk(ram_1_p4),
    .clr(Reset_out));  // open: carry, up
  and and_1 (and_1_out, CS1[17], controlled_buffer_13_out);
  assign ram_1_p1 = or_3_out ? AddressBus : 16'bz;  // Controlled_Buffer controlled_buffer_6
  assign DataBus = CS1[14] ? ram_1_p5 : 16'bz;  // Controlled_Buffer controlled_buffer_7
  assign IQ1Addr_out = not_2_out ? Queue1_q : 16'bz;  // Controlled_Buffer IQ1Addr
  not not_2 (not_2_out, datatypedecoder_1_iq1ad);
  assign IQ1Data_out = datatypedecoder_1_iq1ad ? Queue1_q : 16'bz;  // Controlled_Buffer IQ1Data
  assign IQ2Addr_out = not_3_out ? Queue2_q : 16'bz;  // Controlled_Buffer IQ2Addr
  not not_3 (not_3_out, datatypedecoder_1_iq2ad);
  assign IQ2Data_out = datatypedecoder_1_iq2ad ? Queue2_q : 16'bz;  // Controlled_Buffer IQ2Data
  assign AddressBus = controlled_buffer_1_out ? counter_1_q : 16'bz;  // Controlled_Buffer controlled_buffer_8
  not not_4 (controlled_buffer_1_out, iqctrl_1_stop);
  or or_3 (or_3_out, CS1[13], CS1[14]);
  and and_2 (and_2_out, ram_1_p4, iqctrl_1_stop);
  DataTypeDecoder datatypedecoder_1 (
    .DataType(typedecoderunit_1_datatype), .Stop(and_2_out), .IQ1AD(datatypedecoder_1_iq1ad),
    .IQ2AD(datatypedecoder_1_iq2ad), .IQ1Out(datatypedecoder_1_iq1out), .IQ2Out(datatypedecoder_1_iq2out));
  IQCtrl iqctrl_1 (
    .Reset(Reset_out), .Clock(ram_1_p4), .QueueSize(queuesizedecoder_1_queuesize), .Stop(iqctrl_1_stop),
    .State(iqctrl_1_state));
  Multiplexer #(.width(16)) multiplexer_1 (
    .in1(IQ1Addr_out), .out(AddressBus), .sel(datatypedecoder_1_iq1out));  // open: in0
  Multiplexer #(.width(16)) multiplexer_2 (
    .in1(IQ1Data_out), .out(DataBus), .sel(datatypedecoder_1_iq1out));  // open: in0
  Multiplexer #(.width(16)) multiplexer_3 (
    .in1(IQ2Addr_out), .out(AddressBus), .sel(datatypedecoder_1_iq2out));  // open: in0
  Multiplexer #(.width(16)) multiplexer_4 (
    .in1(IQ2Data_out), .out(DataBus), .sel(datatypedecoder_1_iq2out));  // open: in0
  InstructionTypeDecoder instructiontypedecoder_1 (
    .Arg1(Instruction_q[8:6]), .Arg2(Instruction_q[11:9]),
    .InstructionType(typedecoderunit_1_instructiontype), .RC1(instructiontypedecoder_1_rc1),
    .RC2(instructiontypedecoder_1_rc2), .ALU(instructiontypedecoder_1_alu), .CJ(instructiontypedecoder_1_cj),
    .ERC(instructiontypedecoder_1_erc));
  Clock clock_1 (.out(clock_1_out));
  and and_3 (ram_1_p4, clock_1_out, ~register_1_q);  // AND_Gate
  Pull_Resistor pull_resistor_1 (.node(undriven_2[7]));
  Button Reset (.out(Reset_out));
  DotMatrix #(.matrixcols(24), .matrixrows(16)) dotmatrix_1 (
    .col0(screencontroller_1_d), .col1(screencontroller_1_d_1), .col2(screencontroller_1_d_2),
    .col3(screencontroller_1_d_3), .col4(screencontroller_1_d_4), .col5(screencontroller_1_d_5),
    .col6(screencontroller_1_d_6), .col7(screencontroller_1_d_7), .col8(screencontroller_1_d_8),
    .col9(screencontroller_1_d_9), .col10(screencontroller_1_d_10), .col11(screencontroller_1_d_11),
    .col12(screencontroller_1_d_12), .col13(screencontroller_1_d_13), .col14(screencontroller_1_d_14),
    .col15(screencontroller_1_d_15), .col16(screencontroller_1_d_16), .col17(screencontroller_1_d_17),
    .col18(screencontroller_1_d_18), .col19(screencontroller_1_d_19), .col20(screencontroller_1_d_20),
    .col21(screencontroller_1_d_21), .col22(screencontroller_1_d_22), .col23(screencontroller_1_d_23));
  ScreenController screencontroller_1 (
    .Row(undriven_2[4:0]), .DisplayOut(undriven_2[6]), .DataIn(undriven_4), .WriteIn(undriven_2[5]),
    .Clock(undriven), .Reset(or_4_out), .DataOut(screencontroller_1_dataout), .D(screencontroller_1_d),
    .D_1(screencontroller_1_d_1), .D_2(screencontroller_1_d_2), .D_3(screencontroller_1_d_3),
    .D_4(screencontroller_1_d_4), .D_5(screencontroller_1_d_5), .D_6(screencontroller_1_d_6),
    .D_7(screencontroller_1_d_7), .D_8(screencontroller_1_d_8), .D_9(screencontroller_1_d_9),
    .D_10(screencontroller_1_d_10), .D_11(screencontroller_1_d_11), .D_12(screencontroller_1_d_12),
    .D_13(screencontroller_1_d_13), .D_14(screencontroller_1_d_14), .D_15(screencontroller_1_d_15),
    .D_16(screencontroller_1_d_16), .D_17(screencontroller_1_d_17), .D_18(screencontroller_1_d_18),
    .D_19(screencontroller_1_d_19), .D_20(screencontroller_1_d_20), .D_21(screencontroller_1_d_21),
    .D_22(screencontroller_1_d_22), .D_23(screencontroller_1_d_23));
  or or_4 (or_4_out, undriven_2[7], undriven_3);
  Register #(.trigger("high"), .width(1)) register_1 (
    .D(CS1[10]), .en(CS1[10]), .Q(register_1_q), .clk(ram_1_p4), .clr(Reset_out));
  assign DataBus = CS1[11] ? alu_1_output : 16'bz;  // Controlled_Buffer controlled_buffer_9
  ExtraRegisterController extraregistercontroller_1 (
    .WE(CS1[15]), .OE(CS1[16]), .ERC(instructiontypedecoder_1_erc),
    .ER0_WE_OE(extraregistercontroller_1_er0_we_oe), .ER1_WE_OE(extraregistercontroller_1_er1_we_oe),
    .ER2_WE_OE(extraregistercontroller_1_er2_we_oe), .ER3_WE_OE(extraregistercontroller_1_er3_we_oe),
    .ER4_WE_OE(extraregistercontroller_1_er4_we_oe), .ER5_WE_OE(extraregistercontroller_1_er5_we_oe),
    .ER6_WE_OE(extraregistercontroller_1_er6_we_oe), .ER7_WE_OE(extraregistercontroller_1_er7_we_oe));
  ALU alu_1 (
    .CalcOption(instructiontypedecoder_1_alu), .PortA(RegA_q), .PortB(RegB_q), .Output(alu_1_output),
    .DivRemainder(alu_1_divremainder), .FlagOut(alu_1_flagout));
  Register #(.trigger("falling"), .width(16)) RegA (
    .D(DataBus), .en(extraregistercontroller_1_er0_we_oe[0]), .Q(RegA_q), .clk(ram_1_p4), .clr(Reset_out));
  Register #(.trigger("falling"), .width(16)) RegB (
    .D(DataBus), .en(extraregistercontroller_1_er1_we_oe[0]), .Q(RegB_q), .clk(ram_1_p4), .clr(Reset_out));
  assign DataBus = extraregistercontroller_1_er4_we_oe[1] ? DivOut_q : 16'bz;  // Controlled_Buffer controlled_buffer_10
  assign DataBus = extraregistercontroller_1_er2_we_oe[1] ? register_2_q : 16'bz;  // Controlled_Buffer controlled_buffer_11
  Register #(.trigger("falling"), .width(16)) DivOut (
    .D(alu_1_divremainder), .en(CS1[12]), .Q(DivOut_q), .clk(ram_1_p4), .clr(Reset_out));
  Register #(.trigger("falling"), .width(5)) Flag (
    .D(alu_1_flagout), .en(CS1[12]), .Q(Flag_q), .clk(ram_1_p4), .clr(Reset_out));
  Decoder #(.enable("false"), .select(3)) decoder_1 (
    .out0(decoder_1_out0), .out1(decoder_1_out1[0]), .out2(decoder_1_out1[1]), .out3(decoder_1_out1[2]),
    .out4(decoder_1_out1[3]), .out5(decoder_1_out1[4]), .sel(instructiontypedecoder_1_cj));  // open: out6, out7
  Register #(.width(16)) register_2 (
    .D(DataBus), .en(extraregistercontroller_1_er2_we_oe[0]), .Q(register_2_q), .clk(ram_1_p4), .clr(ram_1_p4));
  assign DataBus = extraregistercontroller_1_er3_we_oe[0] ? register_3_q : 16'bz;  // Controlled_Buffer controlled_buffer_12
  PortUnit portunit_1 (
    .PORTADDRWE(extraregistercontroller_1_er5_we_oe[0]), .PORTRWWE(extraregistercontroller_1_er6_we_oe[0]),
    .PORTEWE(extraregistercontroller_1_er7_we_oe[0]), .Clock(ram_1_p4), .Reset(Reset_out),
    .DataBusIn(DataBus), .PORTWE(CS1[19]), .PORTOE(CS1[20]), .DataBusOut(DataBus),
    .PortC_Out(portunit_1_portc_out));  // open: PortB_In, PortC_In, PortD_In, PortA_In, PortA_Out, PortB_Out, PortD_Out
  RegisterUnit registerunit_1 (
    .RE1(CS1[4]), .RE2(CS1[5]), .OE_WE1(CS1[6]), .OE_WE2(CS1[7]), .DataBus(DataBus), .Reset(Reset_out),
    .ADDR_DATA1(CS1[8]), .ADDR_DATA2(CS1[9]), .ControlSignal1(instructiontypedecoder_1_rc1),
    .ControlSignal2(instructiontypedecoder_1_rc2), .Clock(ram_1_p4), .DataBusOut(DataBus),
    .AddressBusOut(AddressBus));
  assign controlled_buffer_13_out = not_5_out ? or_5_out : 1'bz;  // Controlled_Buffer controlled_buffer_13
  not not_5 (not_5_out, decoder_1_out0);
  assign controlled_buffer_13_out = decoder_1_out0 ? decoder_1_out0 : 1'bz;  // Controlled_Buffer controlled_buffer_14
  Pull_Resistor pull_resistor_2 (.node(decoder_1_out0));
  assign and_4_out = Flag_q & decoder_1_out1;  // AND_Gate and_4, 5 bits wide
  Pull_Resistor pull_resistor_3 (.node(decoder_1_out1));
  Register #(.trigger("falling"), .width(16)) register_3 (
    .D(DataBus), .en(extraregistercontroller_1_er3_we_oe[1]), .Q(register_3_q), .clk(ram_1_p4), .clr(ram_1_p4));
  or or_5 (or_5_out, and_4_out[0], and_4_out[1], and_4_out[2], and_4_out[3], and_4_out[4]);
  Pull_Resistor pull_resistor_4 (.node(portunit_1_portc_out[9]));
  TTY tty_1 (
    .data(portunit_1_portc_out[6:0]), .clk(portunit_1_portc_out[7]), .we(portunit_1_portc_out[8]),
    .clr(or_6_out));
  or or_6 (or_6_out, portunit_1_portc_out[9], Reset_out);

  // Notes on the sheet:
  //   contents of EEPROM (hex, n*v repeats v):
  //   f 10 48 65 6c 6c 6f 2c 20 77 6f 72 6c 64 21 0 1c9 4 189 4 149 2 13 200 2 2 82 0 59 48 49 0 e 4f 33
  //   48 49 180 a4c 52 48 49 7f 84c 52 8 49 1 c f 1c 1f
  //   PCWE/OE
  //   MEMWE/OE
  //   stop
  //   ALUOE
  //   ALUSTORE
  //   WE/OE
  //   1E
  //   2E
  //   1OE/WE
  //   2OE/WE
  //   1A/D
  //   2A/D
  //   Only Div : DataIn
  //   11
  //   WE/OE
  //   Jump is special; it should always make CNR activated if JMP is 1
  //   1, if flag register and given condition is identical
  //   0, if not identical
  //   CNR(Condition Right)
endmodule

module RegisterUnit (
  input  RE1,
  input  RE2,
  input  OE_WE1,
  input  OE_WE2,
  input  [15:0] DataBus,
  input  Reset,
  input  ADDR_DATA1,
  input  ADDR_DATA2,
  input  [2:0] ControlSignal1,
  input  [2:0] ControlSignal2,
  input  Clock,
  output [15:0] DataBusOut,
  output [15:0] AddressBusOut
);

  wire and_1_out, and_2_out, and_3_out, and_4_out, and_5_out, and_6_out, and_7_out, and_8_out, and_9_out,
       and_10_out, and_11_out, and_12_out, and_13_out, and_14_out, and_15_out, and_16_out, and_17_out,
       and_18_out, decoder_1_out0, decoder_1_out1, decoder_1_out2, decoder_1_out3, decoder_1_out4,
       decoder_1_out5, decoder_1_out6, decoder_1_out7, decoder_2_out0, decoder_2_out1, decoder_2_out2,
       decoder_2_out3, decoder_2_out4, decoder_2_out5, decoder_2_out6, decoder_2_out7, or_1_out, or_2_out,
       or_3_out, or_4_out, or_5_out, or_6_out, or_7_out, or_8_out;
  wire [15:0] multiplexer_1_out, multiplexer_2_out, register_1_q, register_2_q, register_3_q, register_4_q,
       register_5_q, register_6_q, register_7_q, register_8_q;

  Decoder #(.select(3)) decoder_1 (
    .out0(decoder_1_out0), .out1(decoder_1_out1), .out2(decoder_1_out2), .out3(decoder_1_out3),
    .out4(decoder_1_out4), .out5(decoder_1_out5), .out6(decoder_1_out6), .out7(decoder_1_out7),
    .sel(ControlSignal1));  // open: en
  Decoder #(.select(3)) decoder_2 (
    .out0(decoder_2_out0), .out1(decoder_2_out1), .out2(decoder_2_out2), .out3(decoder_2_out3),
    .out4(decoder_2_out4), .out5(decoder_2_out5), .out6(decoder_2_out6), .out7(decoder_2_out7),
    .sel(ControlSignal2));  // open: en
  and and_1 (and_1_out, RE1, OE_WE1, decoder_1_out0);
  and and_2 (and_2_out, RE2, OE_WE2, decoder_2_out0);
  and and_3 (and_3_out, RE1, OE_WE1, decoder_1_out1);
  and and_4 (and_4_out, RE2, OE_WE2, decoder_2_out1);
  and and_5 (and_5_out, RE1, OE_WE1, decoder_1_out2);
  and and_6 (and_6_out, RE2, OE_WE2, decoder_2_out2);
  and and_7 (and_7_out, RE1, OE_WE1, decoder_1_out3);
  and and_8 (and_8_out, RE2, OE_WE2, decoder_2_out3);
  and and_9 (and_9_out, RE1, OE_WE1, decoder_1_out4);
  and and_10 (and_10_out, RE2, OE_WE2, decoder_2_out4);
  and and_11 (and_11_out, RE1, OE_WE1, decoder_1_out5);
  and and_12 (and_12_out, RE2, OE_WE2, decoder_2_out5);
  and and_13 (and_13_out, RE1, OE_WE1, decoder_1_out6);
  and and_14 (and_14_out, RE2, OE_WE2, decoder_2_out6);
  and and_15 (and_15_out, RE1, OE_WE1, decoder_1_out7);
  and and_16 (and_16_out, RE2, OE_WE2, decoder_2_out7);
  and and_17 (and_17_out, ~OE_WE1, RE1);  // AND_Gate
  and and_18 (and_18_out, ~OE_WE2, RE2);  // AND_Gate
  or or_1 (or_1_out, and_1_out, and_2_out);
  or or_2 (or_2_out, and_3_out, and_4_out);
  or or_3 (or_3_out, and_5_out, and_6_out);
  or or_4 (or_4_out, and_7_out, and_8_out);
  or or_5 (or_5_out, and_9_out, and_10_out);
  or or_6 (or_6_out, and_11_out, and_12_out);
  or or_7 (or_7_out, and_13_out, and_14_out);
  or or_8 (or_8_out, and_15_out, and_16_out);
  Register #(.trigger("falling"), .width(16)) register_1 (
    .D(DataBus), .en(or_1_out), .Q(register_1_q), .clk(Clock), .clr(Reset));
  Register #(.trigger("falling"), .width(16)) register_2 (
    .D(DataBus), .en(or_2_out), .Q(register_2_q), .clk(Clock), .clr(Reset));
  Register #(.trigger("falling"), .width(16)) register_3 (
    .D(DataBus), .en(or_3_out), .Q(register_3_q), .clk(Clock), .clr(Reset));
  Register #(.trigger("falling"), .width(16)) register_4 (
    .D(DataBus), .en(or_4_out), .Q(register_4_q), .clk(Clock), .clr(Reset));
  Register #(.trigger("falling"), .width(16)) register_5 (
    .D(DataBus), .en(or_5_out), .Q(register_5_q), .clk(Clock), .clr(Reset));
  Register #(.trigger("falling"), .width(16)) register_6 (
    .D(DataBus), .en(or_6_out), .Q(register_6_q), .clk(Clock), .clr(Reset));
  Register #(.trigger("falling"), .width(16)) register_7 (
    .D(DataBus), .en(or_7_out), .Q(register_7_q), .clk(Clock), .clr(Reset));
  Register #(.trigger("falling"), .width(16)) register_8 (
    .D(DataBus), .en(or_8_out), .Q(register_8_q), .clk(Clock), .clr(Reset));
  Multiplexer #(.disabled("Z"), .enable("true"), .select(3), .width(16)) multiplexer_1 (
    .in0(register_1_q), .in1(register_2_q), .in2(register_3_q), .in3(register_4_q), .in4(register_5_q),
    .in5(register_6_q), .in6(register_7_q), .in7(register_8_q), .out(multiplexer_1_out),
    .sel(ControlSignal1), .en(and_17_out));
  Multiplexer #(.disabled("Z"), .enable("true"), .select(3), .width(16)) multiplexer_2 (
    .in0(register_1_q), .in1(register_2_q), .in2(register_3_q), .in3(register_4_q), .in4(register_5_q),
    .in5(register_6_q), .in6(register_7_q), .in7(register_8_q), .out(multiplexer_2_out),
    .sel(ControlSignal2), .en(and_18_out));
  assign DataBusOut = ADDR_DATA1 ? multiplexer_1_out : 16'bz;  // Controlled_Buffer controlled_buffer_1
  Multiplexer #(.width(16)) multiplexer_3 (
    .in0(multiplexer_1_out), .out(AddressBusOut), .sel(ADDR_DATA1));  // open: in1
  assign DataBusOut = ADDR_DATA2 ? multiplexer_2_out : 16'bz;  // Controlled_Buffer controlled_buffer_2
  Multiplexer #(.width(16)) multiplexer_4 (
    .in0(multiplexer_2_out), .out(AddressBusOut), .sel(ADDR_DATA2));  // open: in1
endmodule

module IQCtrl (
  input  Reset,
  input  Clock,
  input  [1:0] QueueSize,
  output Stop,
  output [3:0] State
);

  wire or_1_out, or_2_out;
  wire [3:0] and_1_out, QS;

  D_Flip_Flop d_ff_1 (.clk(Clock), .D(State[3]), .Q(Stop), .preset(or_1_out));  // open: Qn, reset
  D_Flip_Flop d_ff_2 (.clk(Clock), .D(Stop), .Q(State[0]), .reset(or_1_out));  // open: Qn, preset
  or or_1 (or_1_out, Reset, or_2_out);
  D_Flip_Flop d_ff_3 (.clk(Clock), .D(State[0]), .Q(State[1]), .reset(or_1_out));  // open: Qn, preset
  D_Flip_Flop d_ff_4 (.clk(Clock), .D(State[1]), .Q(State[2]), .reset(or_1_out));  // open: Qn, preset
  D_Flip_Flop d_ff_5 (.clk(Clock), .D(State[2]), .Q(State[3]), .reset(or_1_out));  // open: Qn, preset
  Decoder #(.select(2)) decoder_1 (
    .out0(QS[0]), .out1(QS[1]), .out2(QS[2]), .out3(QS[3]), .sel(QueueSize));  // open: en
  assign and_1_out = State & QS;  // AND_Gate and_1, 4 bits wide
  or or_2 (or_2_out, and_1_out[0], and_1_out[1], and_1_out[2], and_1_out[3]);
endmodule

module RegisterController (
  input  [2:0] Reg1,
  input  [2:0] Reg2,
  input  [2:0] InstructionType,
  output [2:0] RC1,
  output [2:0] RC2
);

  wire and_1_out, and_2_out, or_1_out;

  or or_1 (or_1_out, InstructionType[0], InstructionType[1]);
  and and_1 (and_1_out, or_1_out, ~InstructionType[2]);  // AND_Gate
  and and_2 (and_2_out, ~InstructionType[0], InstructionType[1], ~InstructionType[2]);  // AND_Gate
  and and_3 (RC1[0], and_1_out, Reg1[0]);
  and and_4 (RC1[1], and_1_out, Reg1[1]);
  and and_5 (RC1[2], and_1_out, Reg1[2]);
  and and_6 (RC2[0], and_2_out, Reg2[0]);
  and and_7 (RC2[1], and_2_out, Reg2[1]);
  and and_8 (RC2[2], and_2_out, Reg2[2]);
endmodule

module ALU (
  input  [2:0] CalcOption,
  input  [15:0] PortA,
  input  [15:0] PortB,
  output [15:0] Output,
  output [4:0] FlagOut,
  output [15:0] DivRemainder
);

  wire and_3_out;
  wire [2:0] and_1_out;
  wire [15:0] adder_1_out, and_2_out, divider_1_out, divider_1_rem, multiplier_1_out, not_1_out, or_1_out,
       subtractor_1_out, xor_1_out;

  Adder #(.width(16)) adder_1 (.a(PortA), .b(PortB), .out(adder_1_out), .cout(FlagOut[3]));  // open: cin
  assign and_1_out = CalcOption & 3'b011;  // AND_Gate and_1, 3 bits wide
  Subtractor #(.width(16)) subtractor_1 (.a(PortA), .b(PortB), .out(subtractor_1_out));  // open: bin, bout
  Multiplexer #(.select(3), .width(16)) multiplexer_1 (
    .in0(adder_1_out), .in1(subtractor_1_out), .in2(multiplier_1_out), .in3(divider_1_out), .in4(and_2_out),
    .in5(or_1_out), .in6(xor_1_out), .in7(not_1_out), .out({FlagOut[2], Output[14:0]}), .sel(CalcOption));
  Multiplier #(.width(16)) multiplier_1 (.a(PortA), .b(PortB), .out(multiplier_1_out));  // open: cin, cout
  Divider #(.width(16)) divider_1 (.a(PortA), .b(PortB), .out(divider_1_out), .rem(divider_1_rem));  // open: upper
  assign and_2_out = PortB & PortA;  // AND_Gate and_2, 16 bits wide
  assign xor_1_out = PortB ^ PortA;  // XOR_Gate xor_1, 16 bits wide
  assign or_1_out = PortB | PortA;  // OR_Gate or_1, 16 bits wide
  and and_3 (and_3_out, and_1_out[0], and_1_out[2]);
  nor nor_1 (FlagOut[0], Output[0], Output[1], Output[2], Output[3], Output[4], Output[5], Output[6], Output[7], Output[9], Output[10], Output[11], Output[12], Output[13], Output[14], FlagOut[2], Output[8]);
  assign not_1_out = ~PortA;  // NOT_Gate not_1, 16 bits wide
  assign DivRemainder = and_3_out ? divider_1_rem : 16'bz;  // Controlled_Buffer controlled_buffer_1
  not not_2 (FlagOut[1], FlagOut[2]);

  assign Output[15] = FlagOut[2];

  // Notes on the sheet:
  //   Zero
  //   Unsigned
  //   Signed
  //   Carry
  //   Overflow
endmodule

module CentralUnit (
  input  [5:0] Instruction,
  input  OE,
  output [31:0] ControlSignal
);

  wire [5:0] multiplexer_1_out;
  wire [31:0] rom_1_data;

  ROM #(.addrWidth(6), .dataWidth(32)) rom_1 (.addr(multiplexer_1_out), .data(rom_1_data));
  Multiplexer #(.width(6)) multiplexer_1 (.in0({6{1'b0}}), .in1(Instruction), .out(multiplexer_1_out), .sel(OE));
  Multiplexer #(.width(32)) multiplexer_2 (.in0({32{1'b0}}), .in1(rom_1_data), .out(ControlSignal), .sel(OE));

  // Notes on the sheet:
  //   Control Signal
  //   contents of rom_1 (hex, n*v repeats v):
  //   0 270 52 4051 111 4070 2230 2012 8110 8002 c001 c010 1850 5801 1000 20002 20110 24010 80110 80002
  //   84010 80002 104010 100000 100050 200070 200051 0 0 40050 0 400
endmodule

module MemUnit (
  input  [15:0] AddressBus,
  input  [15:0] DataOut,
  input  [15:0] DataBusIn,
  input  WE,
  input  OE,
  input  Clock,
  output [15:0] Address,
  output [15:0] DataIn,
  output [15:0] DataBusOut,
  output ClockOut,
  output ld
);

  wire and_2_out, not_1_out, or_1_out;

  assign Address = or_1_out ? AddressBus : 16'bz;  // Controlled_Buffer MAR
  or or_1 (or_1_out, and_2_out, and_2_out);
  and and_1 (ClockOut, not_1_out, and_2_out);
  not not_1 (not_1_out, Clock);
  assign DataBusOut = ld ? DataOut : 16'bz;  // Controlled_Buffer Out
  assign DataIn = and_2_out ? DataBusIn : 16'bz;  // Controlled_Buffer In
  and and_2 (and_2_out, WE, ~OE);  // AND_Gate
  and and_3 (ld, ~WE, OE);  // AND_Gate
endmodule

module DataTypeDecoder (
  input  [1:0] DataType,
  input  Stop,
  output IQ1AD,
  output IQ2AD,
  output IQ1Out,
  output IQ2Out
);

  wire and_3_out, or_1_out;

  and and_1 (IQ1AD, DataType[1], DataType[0]);
  and and_2 (IQ2AD, DataType[1], ~DataType[0]);  // AND_Gate
  or or_1 (or_1_out, DataType[1], DataType[0]);
  and and_3 (and_3_out, DataType[1], ~DataType[0]);  // AND_Gate
  and and_4 (IQ1Out, or_1_out, Stop);
  and and_5 (IQ2Out, and_3_out, Stop);
endmodule

module QueueSizeDecoder (
  input  [1:0] DataType,
  output [1:0] QueueSize
);

  not not_1 (QueueSize[0], DataType[0]);
  or or_1 (QueueSize[1], DataType[0], DataType[1]);
endmodule

module InstructionTypeDecoder (
  input  [2:0] Arg1,
  input  [2:0] Arg2,
  input  [3:0] InstructionType,
  output [2:0] RC1,
  output [2:0] RC2,
  output [2:0] ALU,
  output [2:0] CJ,
  output [2:0] ERC
);

  wire [4:0] rom_1_data, rom_2_data;

  ROM #(.addrWidth(4), .dataWidth(5)) rom_1 (.addr(InstructionType), .data(rom_1_data));
  assign RC1 = rom_1_data[0] ? Arg1 : 3'bz;  // Controlled_Buffer controlled_buffer_1
  assign RC2 = rom_1_data[1] ? Arg1 : 3'bz;  // Controlled_Buffer controlled_buffer_2
  assign ALU = rom_1_data[2] ? Arg1 : 3'bz;  // Controlled_Buffer controlled_buffer_3
  assign CJ = rom_1_data[3] ? Arg1 : 3'bz;  // Controlled_Buffer controlled_buffer_4
  assign ERC = rom_1_data[4] ? Arg1 : 3'bz;  // Controlled_Buffer controlled_buffer_5
  ROM #(.addrWidth(4), .dataWidth(5)) rom_2 (.addr(InstructionType), .data(rom_2_data));
  assign RC1 = rom_2_data[0] ? Arg2 : 3'bz;  // Controlled_Buffer controlled_buffer_6
  assign RC2 = rom_2_data[1] ? Arg2 : 3'bz;  // Controlled_Buffer controlled_buffer_7
  assign ALU = rom_2_data[2] ? Arg2 : 3'bz;  // Controlled_Buffer controlled_buffer_8
  assign CJ = rom_2_data[3] ? Arg2 : 3'bz;  // Controlled_Buffer controlled_buffer_9
  assign ERC = rom_2_data[4] ? Arg2 : 3'bz;  // Controlled_Buffer controlled_buffer_10

  // Notes on the sheet:
  //   contents of rom_1 (hex, n*v repeats v):
  //   0 5*1 10 8 4
  //   contents of rom_2 (hex, n*v repeats v):
  //   0 0 2 4 8 10
endmodule

module ExtraRegisterController (
  input  WE,
  input  OE,
  input  [2:0] ERC,
  output [1:0] ER0_WE_OE,
  output [1:0] ER1_WE_OE,
  output [1:0] ER2_WE_OE,
  output [1:0] ER3_WE_OE,
  output [1:0] ER4_WE_OE,
  output [1:0] ER5_WE_OE,
  output [1:0] ER6_WE_OE,
  output [1:0] ER7_WE_OE
);

  wire decoder_1_out0, decoder_1_out1, decoder_1_out2, decoder_1_out3, decoder_1_out4, decoder_1_out5,
       decoder_1_out6, decoder_1_out7;
  wire [1:0] and_2_out, and_4_out, and_6_out, and_8_out, and_10_out, and_12_out, and_14_out, and_16_out,
       rom_1_data;

  Decoder #(.enable("false"), .select(3)) decoder_1 (
    .out0(decoder_1_out0), .out1(decoder_1_out1), .out2(decoder_1_out2), .out3(decoder_1_out3),
    .out4(decoder_1_out4), .out5(decoder_1_out5), .out6(decoder_1_out6), .out7(decoder_1_out7), .sel(ERC));
  ROM #(.addrWidth(3), .dataWidth(2)) rom_1 (.addr(ERC), .data(rom_1_data));
  and and_1 (and_2_out[1], OE, decoder_1_out0);
  and and_2 (and_2_out[0], WE, decoder_1_out0);
  and and_3 (and_4_out[1], OE, decoder_1_out1);
  and and_4 (and_4_out[0], WE, decoder_1_out1);
  and and_5 (and_6_out[1], OE, decoder_1_out2);
  and and_6 (and_6_out[0], WE, decoder_1_out2);
  and and_7 (and_8_out[1], OE, decoder_1_out3);
  and and_8 (and_8_out[0], WE, decoder_1_out3);
  and and_9 (and_10_out[1], OE, decoder_1_out4);
  and and_10 (and_10_out[0], WE, decoder_1_out4);
  and and_11 (and_12_out[1], OE, decoder_1_out5);
  and and_12 (and_12_out[0], WE, decoder_1_out5);
  and and_13 (and_14_out[1], OE, decoder_1_out6);
  and and_14 (and_14_out[0], WE, decoder_1_out6);
  and and_15 (and_16_out[1], OE, decoder_1_out7);
  and and_16 (and_16_out[0], WE, decoder_1_out7);
  assign ER0_WE_OE = and_2_out & rom_1_data;  // AND_Gate and_17, 2 bits wide
  assign ER1_WE_OE = and_4_out & rom_1_data;  // AND_Gate and_18, 2 bits wide
  assign ER2_WE_OE = and_6_out & rom_1_data;  // AND_Gate and_19, 2 bits wide
  assign ER3_WE_OE = and_8_out & rom_1_data;  // AND_Gate and_20, 2 bits wide
  assign ER4_WE_OE = and_10_out & rom_1_data;  // AND_Gate and_21, 2 bits wide
  assign ER5_WE_OE = and_12_out & rom_1_data;  // AND_Gate and_22, 2 bits wide
  assign ER6_WE_OE = and_14_out & rom_1_data;  // AND_Gate and_23, 2 bits wide
  assign ER7_WE_OE = and_16_out & rom_1_data;  // AND_Gate and_24, 2 bits wide

  // Notes on the sheet:
  //   contents of rom_1 (hex, n*v repeats v):
  //   1 1 3 3 2 1 1 1
endmodule

module TypeDecoderUnit (
  input  [5:0] Instruction,
  output [1:0] DataType,
  output [3:0] InstructionType
);

  ROM #(.addrWidth(6), .dataWidth(4)) rom_1 (.addr(Instruction), .data(InstructionType));
  ROM #(.addrWidth(6), .dataWidth(2)) rom_2 (.addr(Instruction), .data(DataType));

  // Notes on the sheet:
  //   contents of rom_1 (hex, n*v repeats v):
  //   0 2 1 1 1 2 2 1 5 6 7 6 3 3 8 7 4 4 5 6 5 6 5 6 5 2 1
  //   contents of rom_2 (hex, n*v repeats v):
  //   0 0 3 1 1 0 0 3 0 3 1 0 0 1 0 3 0 0 0 3 0 1 0 1 0 0 1
endmodule

module PortUnit (
  input  [15:0] PortA_In,
  input  PORTWE,
  input  PORTOE,
  input  [15:0] PortB_In,
  input  [15:0] DataBusIn,
  input  [15:0] PortC_In,
  input  PORTADDRWE,
  input  [15:0] PortD_In,
  input  PORTRWWE,
  input  PORTEWE,
  input  Clock,
  input  Reset,
  output [15:0] DataBusOut,
  output [15:0] PortA_Out,
  output [15:0] PortB_Out,
  output [15:0] PortC_Out,
  output [15:0] PortD_Out
);

  wire and_1_out, and_2_out, demultiplexer_1_out0, demultiplexer_1_out1, demultiplexer_1_out2,
       demultiplexer_1_out3, multiplexer_1_out;
  wire [15:0] multiplexer_2_out, register_1_q, register_2_q, register_3_q, register_4_q, register_5_q,
       register_6_q, register_7_q;

  Register #(.trigger("falling"), .width(16)) register_1 (
    .D(DataBusIn), .en(PORTADDRWE), .Q(register_1_q), .clk(Clock), .clr(Reset));
  Register #(.trigger("falling"), .width(16)) register_2 (
    .D(DataBusIn), .en(PORTRWWE), .Q(register_2_q), .clk(Clock), .clr(Reset));
  Register #(.trigger("falling"), .width(16)) register_3 (
    .D(DataBusIn), .en(PORTEWE), .Q(register_3_q), .clk(Clock), .clr(Reset));
  Multiplexer #(.select(2)) multiplexer_1 (
    .in0(register_2_q[0]), .in1(register_2_q[1]), .in2(register_2_q[2]), .in3(register_2_q[3]),
    .out(multiplexer_1_out), .sel(register_1_q[1:0]));
  and and_1 (and_1_out, PORTOE, ~multiplexer_1_out);  // AND_Gate
  assign DataBusOut = and_1_out ? multiplexer_2_out : 16'bz;  // Controlled_Buffer controlled_buffer_1
  and and_2 (and_2_out, PORTWE, multiplexer_1_out);
  Demultiplexer #(.select(2)) demultiplexer_1 (
    .out0(demultiplexer_1_out0), .out1(demultiplexer_1_out1), .out2(demultiplexer_1_out2),
    .out3(demultiplexer_1_out3), .in(and_2_out), .sel(register_1_q[1:0]));
  Multiplexer #(.select(2), .width(16)) multiplexer_2 (
    .in0(PortA_In), .in1(PortB_In), .in2(PortC_In), .in3(PortD_In), .out(multiplexer_2_out),
    .sel(register_1_q[1:0]));
  Register #(.trigger("high"), .width(16)) register_4 (
    .D(DataBusIn), .en(demultiplexer_1_out0), .Q(register_4_q), .clk(Clock), .clr(Reset));
  Register #(.trigger("high"), .width(16)) register_5 (
    .D(DataBusIn), .en(demultiplexer_1_out1), .Q(register_5_q), .clk(Clock), .clr(Reset));
  Register #(.trigger("high"), .width(16)) register_6 (
    .D(DataBusIn), .en(demultiplexer_1_out2), .Q(register_6_q), .clk(Clock), .clr(Reset));
  Register #(.trigger("high"), .width(16)) register_7 (
    .D(DataBusIn), .en(demultiplexer_1_out3), .Q(register_7_q), .clk(Clock), .clr(Reset));
  assign PortA_Out = register_3_q[0] ? register_4_q : 16'bz;  // Controlled_Buffer controlled_buffer_2
  assign PortB_Out = register_3_q[1] ? register_5_q : 16'bz;  // Controlled_Buffer controlled_buffer_3
  assign PortC_Out = register_3_q[2] ? register_6_q : 16'bz;  // Controlled_Buffer controlled_buffer_4
  assign PortD_Out = register_3_q[3] ? register_7_q : 16'bz;  // Controlled_Buffer controlled_buffer_5
endmodule

module ScreenController (
  input  [15:0] DataIn,
  input  WriteIn,
  input  Clock,
  input  Reset,
  input  DisplayOut,
  input  [4:0] Row,
  output [15:0] D,
  output [15:0] D_8,
  output [15:0] D_16,
  output [15:0] DataOut,
  output [15:0] D_1,
  output [15:0] D_9,
  output [15:0] D_17,
  output [15:0] D_2,
  output [15:0] D_10,
  output [15:0] D_18,
  output [15:0] D_3,
  output [15:0] D_11,
  output [15:0] D_19,
  output [15:0] D_4,
  output [15:0] D_12,
  output [15:0] D_20,
  output [15:0] D_5,
  output [15:0] D_13,
  output [15:0] D_21,
  output [15:0] D_6,
  output [15:0] D_14,
  output [15:0] D_22,
  output [15:0] D_7,
  output [15:0] D_15,
  output [15:0] D_23
);

  wire and_1_out, demultiplexer_1_out0, demultiplexer_1_out1, demultiplexer_1_out2, demultiplexer_1_out3,
       demultiplexer_1_out4, demultiplexer_1_out5, demultiplexer_1_out6, demultiplexer_1_out7,
       demultiplexer_1_out8, demultiplexer_1_out9, demultiplexer_1_out10, demultiplexer_1_out11,
       demultiplexer_1_out12, demultiplexer_1_out13, demultiplexer_1_out14, demultiplexer_1_out15,
       demultiplexer_1_out16, demultiplexer_1_out17, demultiplexer_1_out18, demultiplexer_1_out19,
       demultiplexer_1_out20, demultiplexer_1_out21, demultiplexer_1_out22, demultiplexer_1_out23;
  wire [15:0] t1, t2, t3, t4, t5, t6, t7, t8, t9, t10, t11, t12, t13, t14, t15, t16, t17, t18, t19, t20, t21,
       t22, t23, t24;

  Demultiplexer #(.select(5)) demultiplexer_1 (
    .out0(demultiplexer_1_out0), .out1(demultiplexer_1_out1), .out2(demultiplexer_1_out2),
    .out3(demultiplexer_1_out3), .out4(demultiplexer_1_out4), .out5(demultiplexer_1_out5),
    .out6(demultiplexer_1_out6), .out7(demultiplexer_1_out7), .out8(demultiplexer_1_out8),
    .out9(demultiplexer_1_out9), .out10(demultiplexer_1_out10), .out11(demultiplexer_1_out11),
    .out12(demultiplexer_1_out12), .out13(demultiplexer_1_out13), .out14(demultiplexer_1_out14),
    .out15(demultiplexer_1_out15), .out16(demultiplexer_1_out16), .out17(demultiplexer_1_out17),
    .out18(demultiplexer_1_out18), .out19(demultiplexer_1_out19), .out20(demultiplexer_1_out20),
    .out21(demultiplexer_1_out21), .out22(demultiplexer_1_out22), .out23(demultiplexer_1_out23), .in(1'b1),
    .sel(Row));  // open: out24, out25, out26, out27, out28, out29, out30, out31
  and and_1 (and_1_out, WriteIn, Clock);
  Register #(.trigger("falling"), .width(16)) register_1 (
    .D(DataIn), .en(demultiplexer_1_out0), .Q(t1), .clk(and_1_out), .clr(Reset));
  Register #(.trigger("falling"), .width(16)) register_2 (
    .D(DataIn), .en(demultiplexer_1_out1), .Q(t2), .clk(and_1_out), .clr(Reset));
  Register #(.trigger("falling"), .width(16)) register_3 (
    .D(DataIn), .en(demultiplexer_1_out2), .Q(t3), .clk(and_1_out), .clr(Reset));
  Register #(.trigger("falling"), .width(16)) register_4 (
    .D(DataIn), .en(demultiplexer_1_out3), .Q(t4), .clk(and_1_out), .clr(Reset));
  Register #(.trigger("falling"), .width(16)) register_5 (
    .D(DataIn), .en(demultiplexer_1_out4), .Q(t5), .clk(and_1_out), .clr(Reset));
  Register #(.trigger("falling"), .width(16)) register_6 (
    .D(DataIn), .en(demultiplexer_1_out5), .Q(t6), .clk(and_1_out), .clr(Reset));
  Register #(.trigger("falling"), .width(16)) register_7 (
    .D(DataIn), .en(demultiplexer_1_out6), .Q(t7), .clk(and_1_out), .clr(Reset));
  Register #(.trigger("falling"), .width(16)) register_8 (
    .D(DataIn), .en(demultiplexer_1_out7), .Q(t8), .clk(and_1_out), .clr(Reset));
  Register #(.trigger("falling"), .width(16)) register_9 (
    .D(DataIn), .en(demultiplexer_1_out8), .Q(t9), .clk(and_1_out), .clr(Reset));
  Register #(.trigger("falling"), .width(16)) register_10 (
    .D(DataIn), .en(demultiplexer_1_out9), .Q(t10), .clk(and_1_out), .clr(Reset));
  Register #(.trigger("falling"), .width(16)) register_11 (
    .D(DataIn), .en(demultiplexer_1_out10), .Q(t11), .clk(and_1_out), .clr(Reset));
  Register #(.trigger("falling"), .width(16)) register_12 (
    .D(DataIn), .en(demultiplexer_1_out11), .Q(t12), .clk(and_1_out), .clr(Reset));
  Register #(.trigger("falling"), .width(16)) register_13 (
    .D(DataIn), .en(demultiplexer_1_out12), .Q(t13), .clk(and_1_out), .clr(Reset));
  Register #(.trigger("falling"), .width(16)) register_14 (
    .D(DataIn), .en(demultiplexer_1_out13), .Q(t14), .clk(and_1_out), .clr(Reset));
  Register #(.trigger("falling"), .width(16)) register_15 (
    .D(DataIn), .en(demultiplexer_1_out14), .Q(t15), .clk(and_1_out), .clr(Reset));
  Register #(.trigger("falling"), .width(16)) register_16 (
    .D(DataIn), .en(demultiplexer_1_out15), .Q(t16), .clk(and_1_out), .clr(Reset));
  Register #(.trigger("falling"), .width(16)) register_17 (
    .D(DataIn), .en(demultiplexer_1_out16), .Q(t17), .clk(and_1_out), .clr(Reset));
  Register #(.trigger("falling"), .width(16)) register_18 (
    .D(DataIn), .en(demultiplexer_1_out17), .Q(t18), .clk(and_1_out), .clr(Reset));
  Register #(.trigger("falling"), .width(16)) register_19 (
    .D(DataIn), .en(demultiplexer_1_out18), .Q(t19), .clk(and_1_out), .clr(Reset));
  Register #(.trigger("falling"), .width(16)) register_20 (
    .D(DataIn), .en(demultiplexer_1_out19), .Q(t20), .clk(and_1_out), .clr(Reset));
  Register #(.trigger("falling"), .width(16)) register_21 (
    .D(DataIn), .en(demultiplexer_1_out20), .Q(t21), .clk(and_1_out), .clr(Reset));
  Register #(.trigger("falling"), .width(16)) register_22 (
    .D(DataIn), .en(demultiplexer_1_out21), .Q(t22), .clk(and_1_out), .clr(Reset));
  Register #(.trigger("falling"), .width(16)) register_23 (
    .D(DataIn), .en(demultiplexer_1_out22), .Q(t23), .clk(and_1_out), .clr(Reset));
  Register #(.trigger("falling"), .width(16)) register_24 (
    .D(DataIn), .en(demultiplexer_1_out23), .Q(t24), .clk(and_1_out), .clr(Reset));
  Multiplexer #(.select(5), .width(16)) multiplexer_1 (
    .in0(t1), .in1(t2), .in2(t3), .in3(t4), .in4(t5), .in5(t6), .in6(t7), .in7(t8), .in8(t9), .in9(t10),
    .in10(t11), .in11(t12), .in12(t13), .in13(t14), .in14(t15), .in15(t16), .in16(t17), .in17(t18),
    .in18(t19), .in19(t20), .in20(t21), .in21(t22), .in22(t23), .in23(t24), .out(DataOut), .sel(Row));  // open: in24, in25, in26, in27, in28, in29, in30, in31
  Register #(.trigger("falling"), .width(16)) register_25 (.D(t1), .en(DisplayOut), .Q(D), .clk(Clock), .clr(Reset));
  Register #(.trigger("falling"), .width(16)) register_26 (.D(t2), .en(DisplayOut), .Q(D_1), .clk(Clock), .clr(Reset));
  Register #(.trigger("falling"), .width(16)) register_27 (.D(t3), .en(DisplayOut), .Q(D_2), .clk(Clock), .clr(Reset));
  Register #(.trigger("falling"), .width(16)) register_28 (.D(t4), .en(DisplayOut), .Q(D_3), .clk(Clock), .clr(Reset));
  Register #(.trigger("falling"), .width(16)) register_29 (.D(t5), .en(DisplayOut), .Q(D_4), .clk(Clock), .clr(Reset));
  Register #(.trigger("falling"), .width(16)) register_30 (.D(t6), .en(DisplayOut), .Q(D_5), .clk(Clock), .clr(Reset));
  Register #(.trigger("falling"), .width(16)) register_31 (.D(t7), .en(DisplayOut), .Q(D_6), .clk(Clock), .clr(Reset));
  Register #(.trigger("falling"), .width(16)) register_32 (.D(t8), .en(DisplayOut), .Q(D_7), .clk(Clock), .clr(Reset));
  Register #(.trigger("falling"), .width(16)) register_33 (.D(t9), .en(DisplayOut), .Q(D_8), .clk(Clock), .clr(Reset));
  Register #(.trigger("falling"), .width(16)) register_34 (.D(t10), .en(DisplayOut), .Q(D_9), .clk(Clock), .clr(Reset));
  Register #(.trigger("falling"), .width(16)) register_35 (
    .D(t11), .en(DisplayOut), .Q(D_10), .clk(Clock), .clr(Reset));
  Register #(.trigger("falling"), .width(16)) register_36 (
    .D(t12), .en(DisplayOut), .Q(D_11), .clk(Clock), .clr(Reset));
  Register #(.trigger("falling"), .width(16)) register_37 (
    .D(t13), .en(DisplayOut), .Q(D_12), .clk(Clock), .clr(Reset));
  Register #(.trigger("falling"), .width(16)) register_38 (
    .D(t14), .en(DisplayOut), .Q(D_13), .clk(Clock), .clr(Reset));
  Register #(.trigger("falling"), .width(16)) register_39 (
    .D(t15), .en(DisplayOut), .Q(D_14), .clk(Clock), .clr(Reset));
  Register #(.trigger("falling"), .width(16)) register_40 (
    .D(t16), .en(DisplayOut), .Q(D_15), .clk(Clock), .clr(Reset));
  Register #(.trigger("falling"), .width(16)) register_41 (
    .D(t17), .en(DisplayOut), .Q(D_16), .clk(Clock), .clr(Reset));
  Register #(.trigger("falling"), .width(16)) register_42 (
    .D(t18), .en(DisplayOut), .Q(D_17), .clk(Clock), .clr(Reset));
  Register #(.trigger("falling"), .width(16)) register_43 (
    .D(t19), .en(DisplayOut), .Q(D_18), .clk(Clock), .clr(Reset));
  Register #(.trigger("falling"), .width(16)) register_44 (
    .D(t20), .en(DisplayOut), .Q(D_19), .clk(Clock), .clr(Reset));
  Register #(.trigger("falling"), .width(16)) register_45 (
    .D(t21), .en(DisplayOut), .Q(D_20), .clk(Clock), .clr(Reset));
  Register #(.trigger("falling"), .width(16)) register_46 (
    .D(t22), .en(DisplayOut), .Q(D_21), .clk(Clock), .clr(Reset));
  Register #(.trigger("falling"), .width(16)) register_47 (
    .D(t23), .en(DisplayOut), .Q(D_22), .clk(Clock), .clr(Reset));
  Register #(.trigger("falling"), .width(16)) register_48 (
    .D(t24), .en(DisplayOut), .Q(D_23), .clk(Clock), .clr(Reset));
endmodule
