// Logisim project Computer.circ as structural Verilog: 14 circuits, main circuit Main
module Main (
);

  wire and_1_out, and_2_out, and_3_out, and_4_out, clock_1_out, controlled_buffer_1_out,
       controlled_buffer_16_out, DataType_Decoder_iq1a_d, DataType_Decoder_iq1out, DataType_Decoder_iq2a_d,
       DataType_Decoder_iq2out, decoder_1_out0, instructionqueuecontroller_1_stop, not_1_out, not_2_out,
       not_4_out, not_5_out, not_6_out, or_1_out, or_2_out, or_3_out, register_1_q, Reset_out;
  wire [1:0] extraregistercontroller_1_er0_we_oe, extraregistercontroller_1_er1_we_oe,
       extraregistercontroller_1_er2_we_oe, extraregistercontroller_1_er3_we_oe,
       extraregistercontroller_1_er4_we_oe, extraregistercontroller_1_er5_we_oe,
       extraregistercontroller_1_er6_we_oe, extraregistercontroller_1_er7_we_oe, QC_queuesize,
       typedecoderunit_1_out_3;
  wire [2:0] Instr_Type_Decoder_alu, Instr_Type_Decoder_cj, Instr_Type_Decoder_erc, Instr_Type_Decoder_rc1,
       Instr_Type_Decoder_rc2;
  wire [3:0] instructionqueuecontroller_1_state, typedecoderunit_1_out_2;
  wire [4:0] alu_1_flagout, and_5_out, decoder_1_out1, Flag_q;
  wire [15:0] Address_Bus, alu_1_divremainder, alu_1_output, controlled_buffer_2_out,
       controlled_buffer_4_out, controlled_buffer_6_out, Data_Bus, DivOut_q, EEPROM_data, Instruction_q,
       IQ1Addr_out, IQ1Data_out, IQ2Addr_out, IQ2Data_out, portunit_1_porta_out, portunit_1_portb_out,
       Program_Counter_q, Queue_1_q, Queue_2_q, RegA_q, RegB_q, register_2_q, register_3_q,
       screencontroller_1_dataout, screencontroller_1_out_6, screencontroller_1_out_7,
       screencontroller_1_out_8, screencontroller_1_out_9, screencontroller_1_out_10,
       screencontroller_1_out_11, screencontroller_1_out_12, screencontroller_1_out_13,
       screencontroller_1_out_14, screencontroller_1_out_15, screencontroller_1_out_16,
       screencontroller_1_out_17, screencontroller_1_out_18, screencontroller_1_out_19,
       screencontroller_1_out_20, screencontroller_1_out_21, screencontroller_1_out_22,
       screencontroller_1_out_23, screencontroller_1_out_24, screencontroller_1_out_25,
       screencontroller_1_out_26, screencontroller_1_out_27, screencontroller_1_out_28,
       screencontroller_1_out_29;
  wire [31:0] CS1;

  CentralUnit centralunit_1 (.ControlSignal_0_31(CS1), .Instruction(Instruction_q[5:0]), .OE(and_3_out));
  not not_1 (not_1_out, and_2_out);
  assign controlled_buffer_1_out = and_2_out ? not_1_out : 1'bz;  // Controlled_Buffer controlled_buffer_1
  ROM #(.addrWidth(16), .dataWidth(16), .Select("low")) EEPROM (.addr(controlled_buffer_4_out), .data(EEPROM_data));
  assign controlled_buffer_2_out = CS1[13] ? Data_Bus : 16'bz;  // Controlled_Buffer controlled_buffer_2
  RAM #(.addrWidth(16), .dataWidth(16), .Select("low")) RAM (
    .addr(controlled_buffer_6_out), .data(controlled_buffer_2_out), .clk(and_1_out), .ld(not_2_out));  // open: sel, clr
  and and_1 (and_1_out, or_1_out, ~and_4_out);  // AND_Gate
  Register #(.width(16), .trigger("falling"), .Select("low")) Instruction (
    .D(Data_Bus), .en(instructionqueuecontroller_1_state[0]), .Q(Instruction_q), .clk(and_4_out),
    .clr(Reset_out));
  Register #(.width(16), .trigger("falling"), .Select("low")) Queue_1 (
    .D(Data_Bus), .en(instructionqueuecontroller_1_state[1]), .Q(Queue_1_q), .clk(and_4_out), .clr(Reset_out));
  Register #(.width(16), .trigger("falling"), .Select("low")) Queue_2 (
    .D(Data_Bus), .en(instructionqueuecontroller_1_state[2]), .Q(Queue_2_q), .clk(and_4_out), .clr(Reset_out));
  TypeDecoderUnit typedecoderunit_1 (
    .Instruction(Instruction_q[5:0]), .out_2(typedecoderunit_1_out_2), .out_3(typedecoderunit_1_out_3));
  assign Data_Bus = CS1[18] ? Program_Counter_q : 16'bz;  // Controlled_Buffer controlled_buffer_3
  Counter #(.width(16), .max('hffff), .trigger("falling"), .behavior("old")) Program_Counter (
    .load(and_2_out), .D(Data_Bus), .count(controlled_buffer_1_out), .Q(Program_Counter_q), .clk(and_4_out),
    .clr(Reset_out));  // open: carry, preset
  and and_2 (and_2_out, CS1[17], controlled_buffer_16_out);
  assign controlled_buffer_4_out = controlled_buffer_1_out ? Address_Bus : 16'bz;  // Controlled_Buffer controlled_buffer_4
  assign Data_Bus = controlled_buffer_1_out ? EEPROM_data : 16'bz;  // Controlled_Buffer controlled_buffer_5
  assign controlled_buffer_6_out = or_1_out ? Address_Bus : 16'bz;  // Controlled_Buffer controlled_buffer_6
  assign Data_Bus = CS1[14] ? controlled_buffer_2_out : 16'bz;  // Controlled_Buffer controlled_buffer_7
  or or_1 (or_1_out, CS1[13], CS1[14]);
  not not_2 (not_2_out, CS1[13]);
  assign Address_Bus = controlled_buffer_1_out ? Program_Counter_q : 16'bz;  // Controlled_Buffer controlled_buffer_8
  not not_3 (controlled_buffer_1_out, instructionqueuecontroller_1_stop);
  QueueSizeDecoder QC (.DataType(typedecoderunit_1_out_3), .QueueSize(QC_queuesize));
  InstructionQueueController instructionqueuecontroller_1 (
    .Clock(and_4_out), .Reset(Reset_out), .State(instructionqueuecontroller_1_state),
    .Stop(instructionqueuecontroller_1_stop), .QueueSize(QC_queuesize));
  and and_3 (and_3_out, and_4_out, instructionqueuecontroller_1_stop);
  assign IQ1Addr_out = not_4_out ? Queue_1_q : 16'bz;  // Controlled_Buffer IQ1Addr
  not not_4 (not_4_out, DataType_Decoder_iq1a_d);
  assign IQ1Data_out = DataType_Decoder_iq1a_d ? Queue_1_q : 16'bz;  // Controlled_Buffer IQ1Data
  assign IQ2Addr_out = not_5_out ? Queue_2_q : 16'bz;  // Controlled_Buffer IQ2Addr
  not not_5 (not_5_out, DataType_Decoder_iq2a_d);
  assign IQ2Data_out = DataType_Decoder_iq2a_d ? Queue_2_q : 16'bz;  // Controlled_Buffer IQ2Data
  DataTypeDecoder DataType_Decoder (
    .DataType(typedecoderunit_1_out_3), .IQ1A_D(DataType_Decoder_iq1a_d), .IQ2A_D(DataType_Decoder_iq2a_d),
    .IQ1Out(DataType_Decoder_iq1out), .IQ2Out(DataType_Decoder_iq2out), .Stop(and_3_out));
  InstructionTypeDecoder Instr_Type_Decoder (
    .Arg1(Instruction_q[8:6]), .Arg2(Instruction_q[11:9]), .InstructionType(typedecoderunit_1_out_2),
    .RC1(Instr_Type_Decoder_rc1), .RC2(Instr_Type_Decoder_rc2), .ALU(Instr_Type_Decoder_alu),
    .CJ(Instr_Type_Decoder_cj), .ERC(Instr_Type_Decoder_erc));
  assign Address_Bus = DataType_Decoder_iq1out ? IQ1Addr_out : 16'bz;  // Controlled_Buffer controlled_buffer_9
  assign Data_Bus = DataType_Decoder_iq1out ? IQ1Data_out : 16'bz;  // Controlled_Buffer controlled_buffer_10
  assign Address_Bus = DataType_Decoder_iq2out ? IQ2Addr_out : 16'bz;  // Controlled_Buffer controlled_buffer_11
  assign Data_Bus = DataType_Decoder_iq2out ? IQ2Data_out : 16'bz;  // Controlled_Buffer controlled_buffer_12
  Clock clock_1 (.out(clock_1_out));
  Button Reset (.out(Reset_out));
  and and_4 (and_4_out, ~register_1_q, clock_1_out);  // AND_Gate
  Pull_Resistor pull_resistor_1 (.node(Instr_Type_Decoder_alu));
  Register #(.width(1), .trigger("high"), .Select("low")) register_1 (
    .D(CS1[10]), .en(CS1[10]), .Q(register_1_q), .clk(and_4_out), .clr(Reset_out));
  assign Data_Bus = CS1[11] ? alu_1_output : 16'bz;  // Controlled_Buffer controlled_buffer_13
  ExtraRegisterController extraregistercontroller_1 (
    .ERC(Instr_Type_Decoder_erc), .WE(CS1[15]), .OE(CS1[16]),
    .ER0_WE_OE(extraregistercontroller_1_er0_we_oe), .ER1_WE_OE(extraregistercontroller_1_er1_we_oe),
    .ER2_WE_OE(extraregistercontroller_1_er2_we_oe), .ER3_WE_OE(extraregistercontroller_1_er3_we_oe),
    .ER4_WE_OE(extraregistercontroller_1_er4_we_oe), .ER5_WE_OE(extraregistercontroller_1_er5_we_oe),
    .ER6_WE_OE(extraregistercontroller_1_er6_we_oe), .ER7_WE_OE(extraregistercontroller_1_er7_we_oe));
  Register #(.width(16), .trigger("falling"), .Select("low")) RegA (
    .D(Data_Bus), .en(extraregistercontroller_1_er0_we_oe[0]), .Q(RegA_q), .clk(and_4_out), .clr(Reset_out));
  assign Data_Bus = extraregistercontroller_1_er2_we_oe[1] ? register_2_q : 16'bz;  // Controlled_Buffer controlled_buffer_14
  RegisterUnit Register_Unit (
    .ControlSignal_1(Instr_Type_Decoder_rc1), .ControlSignal_2(Instr_Type_Decoder_rc2), .Clock(and_4_out),
    .OE_WE_2(CS1[7]), .RE_1(CS1[4]), .RE_2(CS1[5]), .OE_WE_1(CS1[6]), .Data_Bus(Data_Bus),
    .ADDR_DATA_1(CS1[8]), .ADDR_DATA_2(CS1[9]), .DataBus_Out(Data_Bus), .AddressBus_Out(Address_Bus),
    .Reset(Reset_out));
  assign Data_Bus = extraregistercontroller_1_er4_we_oe[1] ? DivOut_q : 16'bz;  // Controlled_Buffer controlled_buffer_15
  ALU alu_1 (
    .CalcOption(Instr_Type_Decoder_alu), .DivRemainder(alu_1_divremainder), .PortA(RegA_q), .PortB(RegB_q),
    .Output(alu_1_output), .FlagOut(alu_1_flagout));
  Register #(.width(16), .trigger("falling"), .Select("low")) RegB (
    .D(Data_Bus), .en(extraregistercontroller_1_er1_we_oe[0]), .Q(RegB_q), .clk(and_4_out), .clr(Reset_out));
  Register #(.width(16), .Select("low")) register_2 (
    .D(Data_Bus), .en(extraregistercontroller_1_er2_we_oe[0]), .Q(register_2_q), .clk(and_4_out),
    .clr(Reset_out));
  assign controlled_buffer_16_out = decoder_1_out0 ? decoder_1_out0 : 1'bz;  // Controlled_Buffer controlled_buffer_16
  Register #(.width(16), .trigger("falling"), .Select("low")) DivOut (
    .D(alu_1_divremainder), .en(CS1[12]), .Q(DivOut_q), .clk(and_4_out), .clr(Reset_out));
  Register #(.width(5), .trigger("falling"), .Select("low")) Flag (
    .D(alu_1_flagout), .en(CS1[12]), .Q(Flag_q), .clk(and_4_out), .clr(Reset_out));
  Decoder #(.select(3), .enable("false")) decoder_1 (
    .out0(decoder_1_out0), .out1(decoder_1_out1[0]), .out2(decoder_1_out1[1]), .out3(decoder_1_out1[2]),
    .out4(decoder_1_out1[3]), .out5(decoder_1_out1[4]), .sel(Instr_Type_Decoder_cj));  // open: out6, out7
  Register #(.width(16), .trigger("falling"), .Select("low")) register_3 (
    .D(Data_Bus), .en(extraregistercontroller_1_er3_we_oe[0]), .Q(register_3_q), .clk(and_4_out),
    .clr(Reset_out));
  assign Data_Bus = extraregistercontroller_1_er3_we_oe[1] ? register_3_q : 16'bz;  // Controlled_Buffer controlled_buffer_17
  assign controlled_buffer_16_out = not_6_out ? or_2_out : 1'bz;  // Controlled_Buffer controlled_buffer_18
  not not_6 (not_6_out, decoder_1_out0);
  Pull_Resistor pull_resistor_2 (.node(decoder_1_out0));
  assign and_5_out = Flag_q & decoder_1_out1;  // AND_Gate and_5, 5 bits wide
  Pull_Resistor pull_resistor_3 (.node(decoder_1_out1));
  PortUnit portunit_1 (
    .PORTADDRWE(extraregistercontroller_1_er5_we_oe[0]), .PortA_In(screencontroller_1_dataout),
    .PORTWE(CS1[19]), .PORTOE(CS1[20]), .DataBusOut(Data_Bus), .DataBusIn(Data_Bus),
    .PortA_Out(portunit_1_porta_out), .PORTRWWE(extraregistercontroller_1_er6_we_oe[0]),
    .PortB_Out(portunit_1_portb_out), .PORTEWE(extraregistercontroller_1_er7_we_oe[0]), .Clock(and_4_out),
    .Reset(Reset_out));  // open: PortB_In, PortC_In, PortD_In, PortC_Out, PortD_Out
  or or_2 (or_2_out, and_5_out[0], and_5_out[1], and_5_out[2], and_5_out[3], and_5_out[4]);
  Pull_Resistor pull_resistor_4 (.node(portunit_1_portb_out[7]));
  DotMatrix #(.matrixcols(24), .matrixrows(16)) dotmatrix_1 (
    .col0(screencontroller_1_out_6), .col1(screencontroller_1_out_7), .col2(screencontroller_1_out_8),
    .col3(screencontroller_1_out_9), .col4(screencontroller_1_out_10), .col5(screencontroller_1_out_11),
    .col6(screencontroller_1_out_12), .col7(screencontroller_1_out_13), .col8(screencontroller_1_out_14),
    .col9(screencontroller_1_out_15), .col10(screencontroller_1_out_16), .col11(screencontroller_1_out_17),
    .col12(screencontroller_1_out_18), .col13(screencontroller_1_out_19), .col14(screencontroller_1_out_20),
    .col15(screencontroller_1_out_21), .col16(screencontroller_1_out_22), .col17(screencontroller_1_out_23),
    .col18(screencontroller_1_out_24), .col19(screencontroller_1_out_25), .col20(screencontroller_1_out_26),
    .col21(screencontroller_1_out_27), .col22(screencontroller_1_out_28), .col23(screencontroller_1_out_29));
  ScreenController screencontroller_1 (
    .DataIn(portunit_1_porta_out), .Row(portunit_1_portb_out[4:0]), .DataOut(screencontroller_1_dataout),
    .Reset(or_3_out), .WriteIn(portunit_1_portb_out[5]), .out_6(screencontroller_1_out_6),
    .out_7(screencontroller_1_out_7), .out_8(screencontroller_1_out_8), .out_9(screencontroller_1_out_9),
    .out_10(screencontroller_1_out_10), .out_11(screencontroller_1_out_11),
    .out_12(screencontroller_1_out_12), .out_13(screencontroller_1_out_13),
    .out_14(screencontroller_1_out_14), .out_15(screencontroller_1_out_15),
    .out_16(screencontroller_1_out_16), .out_17(screencontroller_1_out_17),
    .out_18(screencontroller_1_out_18), .out_19(screencontroller_1_out_19),
    .out_20(screencontroller_1_out_20), .out_21(screencontroller_1_out_21),
    .out_22(screencontroller_1_out_22), .out_23(screencontroller_1_out_23),
    .out_24(screencontroller_1_out_24), .out_25(screencontroller_1_out_25),
    .out_26(screencontroller_1_out_26), .out_27(screencontroller_1_out_27),
    .out_28(screencontroller_1_out_28), .out_29(screencontroller_1_out_29));
  or or_3 (or_3_out, portunit_1_portb_out[7], Reset_out);

  // Notes on the sheet:
  //   contents of EEPROM (hex, n*v repeats v):
  //   189 0 7 80e 8 49 1 7 f91 8 49 1 7 817 8 49 1 7 f9f 8 49 1 7 215 8 49 1 7 f95 8 49 1 7 89f 8 49 1 7
  //   f95 8 49 1 7 895 8 49 1 7 49f 8 49 1 7 a84 8 49 1 7 91b 8 49 1 7 9 8 49 1 7 15 8 49 1 7 12 8 49 1 7
  //   880 8 49 1 7 f80 8 49 1 7 880 8 49 1 7 480 8 49 1 7 a80 8 49 1 7 900 8 49 1 7 fafa 1f
  //   DataOut
  //   Stop
  //   PCWE/OE
  //   MEMWE/OE
  //   I. Queue Ctrl.
  //   HLT
  //   1WE/OE
  //   2WE/OE
  //   ALUOE
  //   Pulling Control Signal
  //   ALUSTORE
  //   WE/OE
  //   1E
  //   2E
  //   1A/D
  //   2A/D
  //   Only Div : DataIn
  //   11
  //   WE/OE
  //   ERCWE / ERCOE
  //   WE/OE
  //   Jump is special; it should always make CNR activated if JMP is 1
  //   Row
  //   Write
  //   Reset
  //   CNR(Condition Right)
  //   1, if flag register and given condition is identical
  //   0, if not identical
endmodule

module RegisterUnit (
  input  RE_1,
  input  RE_2,
  input  OE_WE_1,
  input  OE_WE_2,
  input  [15:0] Data_Bus,
  input  Reset,
  input  ADDR_DATA_1,
  input  ADDR_DATA_2,
  input  [2:0] ControlSignal_1,
  input  [2:0] ControlSignal_2,
  input  Clock,
  output [15:0] DataBus_Out,
  output [15:0] AddressBus_Out
);

  wire and_1_out, and_2_out, and_3_out, and_4_out, and_5_out, and_6_out, and_7_out, and_8_out, and_9_out,
       and_10_out, and_11_out, and_12_out, and_13_out, and_14_out, and_15_out, and_16_out, and_17_out,
       and_18_out, decoder_1_out0, decoder_1_out1, decoder_1_out2, decoder_1_out3, decoder_1_out4,
       decoder_1_out5, decoder_1_out6, decoder_1_out7, decoder_2_out0, decoder_2_out1, decoder_2_out2,
       decoder_2_out3, decoder_2_out4, decoder_2_out5, decoder_2_out6, decoder_2_out7, not_1_out, not_2_out,
       or_1_out, or_2_out, or_3_out, or_4_out, or_5_out, or_6_out, or_7_out, or_8_out;
  wire [15:0] multiplexer_1_out, multiplexer_2_out, register_1_q, register_2_q, register_3_q, register_4_q,
       register_5_q, register_6_q, register_7_q, register_8_q;

  Decoder #(.select(3)) decoder_1 (
    .out0(decoder_1_out0), .out1(decoder_1_out1), .out2(decoder_1_out2), .out3(decoder_1_out3),
    .out4(decoder_1_out4), .out5(decoder_1_out5), .out6(decoder_1_out6), .out7(decoder_1_out7),
    .sel(ControlSignal_1));  // open: en
  Decoder #(.select(3)) decoder_2 (
    .out0(decoder_2_out0), .out1(decoder_2_out1), .out2(decoder_2_out2), .out3(decoder_2_out3),
    .out4(decoder_2_out4), .out5(decoder_2_out5), .out6(decoder_2_out6), .out7(decoder_2_out7),
    .sel(ControlSignal_2));  // open: en
  and and_1 (and_1_out, RE_1, OE_WE_1, decoder_1_out0);
  and and_2 (and_2_out, RE_2, OE_WE_2, decoder_2_out0);
  and and_3 (and_3_out, RE_1, OE_WE_1, decoder_1_out1);
  and and_4 (and_4_out, RE_2, OE_WE_2, decoder_2_out1);
  and and_5 (and_5_out, RE_1, OE_WE_1, decoder_1_out2);
  and and_6 (and_6_out, RE_2, OE_WE_2, decoder_2_out2);
  and and_7 (and_7_out, RE_1, OE_WE_1, decoder_1_out3);
  and and_8 (and_8_out, RE_2, OE_WE_2, decoder_2_out3);
  and and_9 (and_9_out, RE_1, OE_WE_1, decoder_1_out4);
  and and_10 (and_10_out, RE_2, OE_WE_2, decoder_2_out4);
  and and_11 (and_11_out, RE_1, OE_WE_1, decoder_1_out5);
  and and_12 (and_12_out, RE_2, OE_WE_2, decoder_2_out5);
  and and_13 (and_13_out, RE_1, OE_WE_1, decoder_1_out6);
  and and_14 (and_14_out, RE_2, OE_WE_2, decoder_2_out6);
  and and_15 (and_15_out, RE_1, OE_WE_1, decoder_1_out7);
  and and_16 (and_16_out, RE_2, OE_WE_2, decoder_2_out7);
  and and_17 (and_17_out, ~OE_WE_1, RE_1);  // AND_Gate
  and and_18 (and_18_out, ~OE_WE_2, RE_2);  // AND_Gate
  or or_1 (or_1_out, and_1_out, and_2_out);
  or or_2 (or_2_out, and_3_out, and_4_out);
  or or_3 (or_3_out, and_5_out, and_6_out);
  or or_4 (or_4_out, and_7_out, and_8_out);
  or or_5 (or_5_out, and_9_out, and_10_out);
  or or_6 (or_6_out, and_11_out, and_12_out);
  or or_7 (or_7_out, and_13_out, and_14_out);
  or or_8 (or_8_out, and_15_out, and_16_out);
  Register #(.width(16), .trigger("falling"), .Select("low")) register_1 (
    .D(Data_Bus), .en(or_1_out), .Q(register_1_q), .clk(Clock), .clr(Reset));
  Register #(.width(16), .trigger("falling"), .Select("low")) register_2 (
    .D(Data_Bus), .en(or_2_out), .Q(register_2_q), .clk(Clock), .clr(Reset));
  Register #(.width(16), .trigger("falling"), .Select("low")) register_3 (
    .D(Data_Bus), .en(or_3_out), .Q(register_3_q), .clk(Clock), .clr(Reset));
  Register #(.width(16), .trigger("falling"), .Select("low")) register_4 (
    .D(Data_Bus), .en(or_4_out), .Q(register_4_q), .clk(Clock), .clr(Reset));
  Register #(.width(16), .trigger("falling"), .Select("low")) register_5 (
    .D(Data_Bus), .en(or_5_out), .Q(register_5_q), .clk(Clock), .clr(Reset));
  Register #(.width(16), .trigger("falling"), .Select("low")) register_6 (
    .D(Data_Bus), .en(or_6_out), .Q(register_6_q), .clk(Clock), .clr(Reset));
  Register #(.width(16), .trigger("falling"), .Select("low")) register_7 (
    .D(Data_Bus), .en(or_7_out), .Q(register_7_q), .clk(Clock), .clr(Reset));
  Register #(.width(16), .trigger("falling"), .Select("low")) register_8 (
    .D(Data_Bus), .en(or_8_out), .Q(register_8_q), .clk(Clock), .clr(Reset));
  Multiplexer #(.select(3), .width(16)) multiplexer_1 (
    .in0(register_1_q), .in1(register_2_q), .in2(register_3_q), .in3(register_4_q), .in4(register_5_q),
    .in5(register_6_q), .in6(register_7_q), .in7(register_8_q), .out(multiplexer_1_out),
    .sel(ControlSignal_1), .en(and_17_out));
  Multiplexer #(.select(3), .width(16)) multiplexer_2 (
    .in0(register_1_q), .in1(register_2_q), .in2(register_3_q), .in3(register_4_q), .in4(register_5_q),
    .in5(register_6_q), .in6(register_7_q), .in7(register_8_q), .out(multiplexer_2_out),
    .sel(ControlSignal_2), .en(and_18_out));
  assign DataBus_Out = ADDR_DATA_1 ? multiplexer_1_out : 16'bz;  // Controlled_Buffer controlled_buffer_1
  assign AddressBus_Out = not_1_out ? multiplexer_1_out : 16'bz;  // Controlled_Buffer controlled_buffer_2
  not not_1 (not_1_out, ADDR_DATA_1);
  assign DataBus_Out = ADDR_DATA_2 ? multiplexer_2_out : 16'bz;  // Controlled_Buffer controlled_buffer_3
  assign AddressBus_Out = not_2_out ? multiplexer_2_out : 16'bz;  // Controlled_Buffer controlled_buffer_4
  not not_2 (not_2_out, ADDR_DATA_2);

  // Other names for the same wires on the sheet: Control_Signal_1[2:0] = ControlSignal_1;
  //   Control_Signal_2[2:0] = ControlSignal_2
endmodule

module InstructionQueueController (
  input  Reset,
  input  Clock,
  input  [1:0] QueueSize,
  output Stop,
  output [3:0] State
);

  wire or_1_out, or_2_out;
  wire [3:0] and_1_out, QS;

  D_Flip_Flop #(.Pre_Clr_Positions("LEGACY"), .enable("true"), .NewFFLayout("false")) d_ff_1 (
    .clk(Clock), .D(State[3]), .Q(Stop), .preset(or_1_out));  // open: Qn, en, reset
  D_Flip_Flop #(.Pre_Clr_Positions("LEGACY"), .enable("true"), .NewFFLayout("false")) d_ff_2 (
    .clk(Clock), .D(Stop), .Q(State[0]), .reset(or_1_out));  // open: Qn, preset, en
  or or_1 (or_1_out, Reset, or_2_out);
  D_Flip_Flop #(.Pre_Clr_Positions("LEGACY"), .enable("true"), .NewFFLayout("false")) d_ff_3 (
    .clk(Clock), .D(State[0]), .Q(State[1]), .reset(or_1_out));  // open: Qn, preset, en
  D_Flip_Flop #(.Pre_Clr_Positions("LEGACY"), .enable("true"), .NewFFLayout("false")) d_ff_4 (
    .clk(Clock), .D(State[1]), .Q(State[2]), .reset(or_1_out));  // open: Qn, preset, en
  D_Flip_Flop #(.Pre_Clr_Positions("LEGACY"), .enable("true"), .NewFFLayout("false")) d_ff_5 (
    .clk(Clock), .D(State[2]), .Q(State[3]), .reset(or_1_out));  // open: Qn, preset, en
  Decoder #(.select(2)) decoder_1 (
    .out0(QS[0]), .out1(QS[1]), .out2(QS[2]), .out3(QS[3]), .sel(QueueSize));  // open: en
  assign and_1_out = State & QS;  // AND_Gate and_1, 4 bits wide
  or or_2 (or_2_out, and_1_out[0], and_1_out[1], and_1_out[2], and_1_out[3]);
endmodule

module RegisterController (
  input  [2:0] Reg1,
  input  [2:0] Reg2,
  input  [2:0] InstructionType,
  output [2:0] RC1,
  output [2:0] RC2
);

  wire and_1_out, and_2_out, or_1_out;

  or or_1 (or_1_out, InstructionType[0], InstructionType[1]);
  and and_1 (and_1_out, or_1_out, ~InstructionType[2]);  // AND_Gate
  and and_2 (and_2_out, ~InstructionType[0], InstructionType[1], ~InstructionType[2]);  // AND_Gate
  and and_3 (RC1[0], and_1_out, Reg1[0]);
  and and_4 (RC1[1], and_1_out, Reg1[1]);
  and and_5 (RC1[2], and_1_out, Reg1[2]);
  and and_6 (RC2[0], and_2_out, Reg2[0]);
  and and_7 (RC2[1], and_2_out, Reg2[1]);
  and and_8 (RC2[2], and_2_out, Reg2[2]);
endmodule

module ALU (
  input  [2:0] CalcOption,
  input  [15:0] PortA,
  input  [15:0] PortB,
  output [15:0] Output,
  output [4:0] FlagOut,
  output [15:0] DivRemainder
);

  wire and_3_out;
  wire [2:0] and_1_out;
  wire [15:0] adder_1_out, and_2_out, divider_1_out, divider_1_rem, multiplier_1_out, not_1_out, or_1_out,
       subtractor_1_out, xor_1_out;

  Adder #(.width(16)) adder_1 (.a(PortA), .b(PortB), .out(adder_1_out), .cout(FlagOut[3]));  // open: cin
  assign and_1_out = CalcOption & 3'b011;  // AND_Gate and_1, 3 bits wide
  Subtractor #(.width(16)) subtractor_1 (.a(PortA), .b(PortB), .out(subtractor_1_out));  // open: bin, bout
  Multiplexer #(.select(3), .width(16)) multiplexer_1 (
    .in0(adder_1_out), .in1(subtractor_1_out), .in2(multiplier_1_out), .in3(divider_1_out), .in4(and_2_out),
    .in5(or_1_out), .in6(xor_1_out), .in7(not_1_out), .out({FlagOut[2], Output[14:0]}), .sel(CalcOption));  // open: en
  Multiplier #(.width(16)) multiplier_1 (.a(PortA), .b(PortB), .out(multiplier_1_out));  // open: cin, cout
  Divider #(.width(16)) divider_1 (.a(PortA), .b(PortB), .out(divider_1_out), .rem(divider_1_rem));  // open: upper
  assign and_2_out = PortB & PortA;  // AND_Gate and_2, 16 bits wide
  assign xor_1_out = PortB ^ PortA;  // XOR_Gate xor_1, 16 bits wide
  assign or_1_out = PortB | PortA;  // OR_Gate or_1, 16 bits wide
  and and_3 (and_3_out, and_1_out[0], and_1_out[2]);
  nor nor_1 (FlagOut[0], Output[0], Output[1], Output[2], Output[3], Output[4], Output[5], Output[6], Output[7], Output[9], Output[10], Output[11], Output[12], Output[13], Output[14], FlagOut[2], Output[8]);
  assign not_1_out = ~PortA;  // NOT_Gate not_1, 16 bits wide
  assign DivRemainder = and_3_out ? divider_1_rem : 16'bz;  // Controlled_Buffer controlled_buffer_1
  not not_2 (FlagOut[1], FlagOut[2]);
  Pull_Resistor pull_resistor_1 (.node(FlagOut[4]));

  assign Output[15] = FlagOut[2];

  // Notes on the sheet:
  //   Zero
  //   Unsigned
  //   Signed
  //   Carry
  //   Overflow
endmodule

module CentralUnit (
  input  [5:0] Instruction,
  input  OE,
  output [31:0] ControlSignal_0_31
);

  wire [5:0] multiplexer_1_out;
  wire [31:0] rom_1_data;

  Multiplexer #(.width(6), .enable("false")) multiplexer_1 (
    .in0({6{1'b0}}), .in1(Instruction), .out(multiplexer_1_out), .sel(OE));
  ROM #(.addrWidth(6), .dataWidth(32), .Select("high")) rom_1 (.addr(multiplexer_1_out), .data(rom_1_data));
  Multiplexer #(.width(32), .enable("false")) multiplexer_2 (
    .in0({32{1'b0}}), .in1(rom_1_data), .out(ControlSignal_0_31), .sel(OE));

  // Notes on the sheet:
  //   Control Signal
  //   contents of rom_1 (hex, n*v repeats v):
  //   0 270 52 4051 111 4070 2230 2012 8110 8002 c001 c010 1850 5801 1000 20002 20110 24010 80110 80002
  //   84010 80002 104010 100000 100050 4*0 40050 0 400
endmodule

module MemUnit (
  input  [15:0] AddressBus,
  input  [15:0] DataOut,
  input  [15:0] DataBusIn,
  input  WE,
  input  OE,
  input  Clock,
  output [15:0] Address,
  output [15:0] DataIn,
  output [15:0] DataBusOut,
  output ClockOut,
  output ld
);

  wire and_2_out, not_1_out, or_1_out;

  assign Address = or_1_out ? AddressBus : 16'bz;  // Controlled_Buffer MAR
  or or_1 (or_1_out, and_2_out, and_2_out);
  and and_1 (ClockOut, not_1_out, and_2_out);
  not not_1 (not_1_out, Clock);
  assign DataBusOut = ld ? DataOut : 16'bz;  // Controlled_Buffer Out
  assign DataIn = and_2_out ? DataBusIn : 16'bz;  // Controlled_Buffer In
  and and_2 (and_2_out, WE, ~OE);  // AND_Gate
  and and_3 (ld, ~WE, OE);  // AND_Gate
endmodule

module DataTypeDecoder (
  input  [1:0] DataType,
  input  Stop,
  output IQ1A_D,
  output IQ2A_D,
  output IQ1Out,
  output IQ2Out
);

  wire and_3_out, or_1_out;

  and and_1 (IQ1A_D, DataType[1], DataType[0]);
  and and_2 (IQ2A_D, DataType[1], ~DataType[0]);  // AND_Gate
  or or_1 (or_1_out, DataType[1], DataType[0]);
  and and_3 (and_3_out, DataType[1], ~DataType[0]);  // AND_Gate
  and and_4 (IQ1Out, or_1_out, Stop);
  and and_5 (IQ2Out, and_3_out, Stop);
endmodule

module QueueSizeDecoder (
  input  [1:0] DataType,
  output [1:0] QueueSize
);

  not not_1 (QueueSize[0], DataType[0]);
  or or_1 (QueueSize[1], DataType[0], DataType[1]);
endmodule

module InstructionTypeDecoder (
  input  [2:0] Arg1,
  input  [2:0] Arg2,
  input  [3:0] InstructionType,
  output [2:0] RC1,
  output [2:0] RC2,
  output [2:0] ALU,
  output [2:0] CJ,
  output [2:0] ERC
);

  wire [4:0] rom_1_data, rom_2_data;

  assign RC1 = rom_1_data[0] ? Arg1 : 3'bz;  // Controlled_Buffer controlled_buffer_1
  assign RC2 = rom_1_data[1] ? Arg1 : 3'bz;  // Controlled_Buffer controlled_buffer_2
  assign ALU = rom_1_data[2] ? Arg1 : 3'bz;  // Controlled_Buffer controlled_buffer_3
  assign CJ = rom_1_data[3] ? Arg1 : 3'bz;  // Controlled_Buffer controlled_buffer_4
  assign ERC = rom_1_data[4] ? Arg1 : 3'bz;  // Controlled_Buffer controlled_buffer_5
  ROM #(.addrWidth(4), .dataWidth(5), .Select("low")) rom_1 (.addr(InstructionType), .data(rom_1_data));
  assign RC1 = rom_2_data[0] ? Arg2 : 3'bz;  // Controlled_Buffer controlled_buffer_6
  assign RC2 = rom_2_data[1] ? Arg2 : 3'bz;  // Controlled_Buffer controlled_buffer_7
  assign ALU = rom_2_data[2] ? Arg2 : 3'bz;  // Controlled_Buffer controlled_buffer_8
  assign CJ = rom_2_data[3] ? Arg2 : 3'bz;  // Controlled_Buffer controlled_buffer_9
  assign ERC = rom_2_data[4] ? Arg2 : 3'bz;  // Controlled_Buffer controlled_buffer_10
  ROM #(.addrWidth(4), .dataWidth(5), .Select("low")) rom_2 (.addr(InstructionType), .data(rom_2_data));

  // Notes on the sheet:
  //   contents of rom_1 (hex, n*v repeats v):
  //   0 5*1 10 8 4
  //   contents of rom_2 (hex, n*v repeats v):
  //   0 0 2 4 8 10
endmodule

module ExtraRegisterController (
  input  WE,
  input  OE,
  input  [2:0] ERC,
  output [1:0] ER0_WE_OE,
  output [1:0] ER1_WE_OE,
  output [1:0] ER2_WE_OE,
  output [1:0] ER3_WE_OE,
  output [1:0] ER4_WE_OE,
  output [1:0] ER5_WE_OE,
  output [1:0] ER6_WE_OE,
  output [1:0] ER7_WE_OE
);

  wire decoder_1_out0, decoder_1_out1, decoder_1_out2, decoder_1_out3, decoder_1_out4, decoder_1_out5,
       decoder_1_out6, decoder_1_out7;
  wire [1:0] and_2_out, and_4_out, and_6_out, and_8_out, and_10_out, and_12_out, and_14_out, and_16_out,
       rom_1_data;

  Decoder #(.select(3), .enable("false")) decoder_1 (
    .out0(decoder_1_out0), .out1(decoder_1_out1), .out2(decoder_1_out2), .out3(decoder_1_out3),
    .out4(decoder_1_out4), .out5(decoder_1_out5), .out6(decoder_1_out6), .out7(decoder_1_out7), .sel(ERC));
  ROM #(.addrWidth(3), .dataWidth(2), .Select("low")) rom_1 (.addr(ERC), .data(rom_1_data));
  and and_1 (and_2_out[1], OE, decoder_1_out0);
  and and_2 (and_2_out[0], WE, decoder_1_out0);
  and and_3 (and_4_out[1], OE, decoder_1_out1);
  and and_4 (and_4_out[0], WE, decoder_1_out1);
  and and_5 (and_6_out[1], OE, decoder_1_out2);
  and and_6 (and_6_out[0], WE, decoder_1_out2);
  and and_7 (and_8_out[1], OE, decoder_1_out3);
  and and_8 (and_8_out[0], WE, decoder_1_out3);
  and and_9 (and_10_out[1], OE, decoder_1_out4);
  and and_10 (and_10_out[0], WE, decoder_1_out4);
  and and_11 (and_12_out[1], OE, decoder_1_out5);
  and and_12 (and_12_out[0], WE, decoder_1_out5);
  and and_13 (and_14_out[1], OE, decoder_1_out6);
  and and_14 (and_14_out[0], WE, decoder_1_out6);
  and and_15 (and_16_out[1], OE, decoder_1_out7);
  and and_16 (and_16_out[0], WE, decoder_1_out7);
  assign ER0_WE_OE = and_2_out & rom_1_data;  // AND_Gate and_17, 2 bits wide
  assign ER1_WE_OE = and_4_out & rom_1_data;  // AND_Gate and_18, 2 bits wide
  assign ER2_WE_OE = and_6_out & rom_1_data;  // AND_Gate and_19, 2 bits wide
  assign ER3_WE_OE = and_8_out & rom_1_data;  // AND_Gate and_20, 2 bits wide
  assign ER4_WE_OE = and_10_out & rom_1_data;  // AND_Gate and_21, 2 bits wide
  assign ER5_WE_OE = and_12_out & rom_1_data;  // AND_Gate and_22, 2 bits wide
  assign ER6_WE_OE = and_14_out & rom_1_data;  // AND_Gate and_23, 2 bits wide
  assign ER7_WE_OE = and_16_out & rom_1_data;  // AND_Gate and_24, 2 bits wide

  // Notes on the sheet:
  //   contents of rom_1 (hex, n*v repeats v):
  //   1 1 3 3 2 1 1 1
endmodule

module TypeDecoderUnit (
  input  [5:0] Instruction,
  output [3:0] out_2,
  output [1:0] out_3
);

  ROM #(.addrWidth(6), .dataWidth(4), .Select("low")) rom_1 (.addr(Instruction), .data(out_2));
  ROM #(.addrWidth(6), .dataWidth(2), .Select("low")) rom_2 (.addr(Instruction), .data(out_3));

  // Notes on the sheet:
  //   Instruction Type
  //   contents of rom_1 (hex, n*v repeats v):
  //   0 2 1 1 1 2 2 1 5 6 7 6 3 3 8 7 4 4 5 6 5 6 5 6 5 4*0 1
  //   Data Type
  //   Instruction Type
  //   contents of rom_2 (hex, n*v repeats v):
  //   0 0 3 1 1 0 0 3 0 3 1 0 0 1 0 3 0 0 0 3 0 1 0 1
  //   Data Type
endmodule

module PortUnit (
  input  [15:0] PortA_In,
  input  PORTWE,
  input  PORTOE,
  input  [15:0] PortB_In,
  input  [15:0] DataBusIn,
  input  [15:0] PortC_In,
  input  PORTADDRWE,
  input  [15:0] PortD_In,
  input  PORTRWWE,
  input  PORTEWE,
  input  Clock,
  input  Reset,
  output [15:0] DataBusOut,
  output [15:0] PortA_Out,
  output [15:0] PortB_Out,
  output [15:0] PortC_Out,
  output [15:0] PortD_Out
);

  wire and_1_out, and_2_out, demultiplexer_1_out0, demultiplexer_1_out1, demultiplexer_1_out2,
       demultiplexer_1_out3, multiplexer_1_out;
  wire [15:0] multiplexer_2_out, register_1_q, register_2_q, register_3_q, register_4_q, register_5_q,
       register_6_q, register_7_q;

  Register #(.width(16), .trigger("falling"), .Select("low")) register_1 (
    .D(DataBusIn), .en(PORTADDRWE), .Q(register_1_q), .clk(Clock), .clr(Reset));
  Register #(.width(16), .trigger("falling"), .Select("low")) register_2 (
    .D(DataBusIn), .en(PORTRWWE), .Q(register_2_q), .clk(Clock), .clr(Reset));
  Register #(.width(16), .trigger("falling"), .Select("low")) register_3 (
    .D(DataBusIn), .en(PORTEWE), .Q(register_3_q), .clk(Clock), .clr(Reset));
  Multiplexer #(.select(2), .enable("false")) multiplexer_1 (
    .in0(register_2_q[0]), .in1(register_2_q[1]), .in2(register_2_q[2]), .in3(register_2_q[3]),
    .out(multiplexer_1_out), .sel(register_1_q[1:0]));
  and and_1 (and_1_out, PORTOE, ~multiplexer_1_out);  // AND_Gate
  assign DataBusOut = and_1_out ? multiplexer_2_out : 16'bz;  // Controlled_Buffer controlled_buffer_1
  and and_2 (and_2_out, PORTWE, multiplexer_1_out);
  Demultiplexer #(.select(2), .enable("false")) demultiplexer_1 (
    .out0(demultiplexer_1_out0), .out1(demultiplexer_1_out1), .out2(demultiplexer_1_out2),
    .out3(demultiplexer_1_out3), .in(and_2_out), .sel(register_1_q[1:0]));
  Multiplexer #(.select(2), .width(16), .enable("false")) multiplexer_2 (
    .in0(PortA_In), .in1(PortB_In), .in2(PortC_In), .in3(PortD_In), .out(multiplexer_2_out),
    .sel(register_1_q[1:0]));
  Register #(.width(16), .trigger("high"), .Select("low")) register_4 (
    .D(DataBusIn), .en(demultiplexer_1_out0), .Q(register_4_q), .clk(Clock), .clr(Reset));
  Register #(.width(16), .trigger("high"), .Select("low")) register_5 (
    .D(DataBusIn), .en(demultiplexer_1_out1), .Q(register_5_q), .clk(Clock), .clr(Reset));
  Register #(.width(16), .trigger("high"), .Select("low")) register_6 (
    .D(DataBusIn), .en(demultiplexer_1_out2), .Q(register_6_q), .clk(Clock), .clr(Reset));
  Register #(.width(16), .trigger("high"), .Select("low")) register_7 (
    .D(DataBusIn), .en(demultiplexer_1_out3), .Q(register_7_q), .clk(Clock), .clr(Reset));
  assign PortA_Out = register_3_q[0] ? register_4_q : 16'bz;  // Controlled_Buffer controlled_buffer_2
  assign PortB_Out = register_3_q[1] ? register_5_q : 16'bz;  // Controlled_Buffer controlled_buffer_3
  assign PortC_Out = register_3_q[2] ? register_6_q : 16'bz;  // Controlled_Buffer controlled_buffer_4
  assign PortD_Out = register_3_q[3] ? register_7_q : 16'bz;  // Controlled_Buffer controlled_buffer_5
endmodule

module ScreenController (
  input  [15:0] DataIn,
  input  WriteIn,
  input  Reset,
  input  [4:0] Row,
  output [15:0] DataOut,
  output [15:0] out_6,
  output [15:0] out_7,
  output [15:0] out_8,
  output [15:0] out_9,
  output [15:0] out_10,
  output [15:0] out_11,
  output [15:0] out_12,
  output [15:0] out_13,
  output [15:0] out_14,
  output [15:0] out_15,
  output [15:0] out_16,
  output [15:0] out_17,
  output [15:0] out_18,
  output [15:0] out_19,
  output [15:0] out_20,
  output [15:0] out_21,
  output [15:0] out_22,
  output [15:0] out_23,
  output [15:0] out_24,
  output [15:0] out_25,
  output [15:0] out_26,
  output [15:0] out_27,
  output [15:0] out_28,
  output [15:0] out_29
);

  wire demultiplexer_1_out0, demultiplexer_1_out1, demultiplexer_1_out2, demultiplexer_1_out3,
       demultiplexer_1_out4, demultiplexer_1_out5, demultiplexer_1_out6, demultiplexer_1_out7,
       demultiplexer_1_out8, demultiplexer_1_out9, demultiplexer_1_out10, demultiplexer_1_out11,
       demultiplexer_1_out12, demultiplexer_1_out13, demultiplexer_1_out14, demultiplexer_1_out15,
       demultiplexer_1_out16, demultiplexer_1_out17, demultiplexer_1_out18, demultiplexer_1_out19,
       demultiplexer_1_out20, demultiplexer_1_out21, demultiplexer_1_out22, demultiplexer_1_out23;
  wire [15:0] pull_resistor_1_node, pull_resistor_2_node, pull_resistor_3_node, pull_resistor_4_node,
       pull_resistor_5_node, pull_resistor_6_node, pull_resistor_7_node, pull_resistor_8_node;

  Demultiplexer #(.select(5), .enable("false")) demultiplexer_1 (
    .out0(demultiplexer_1_out0), .out1(demultiplexer_1_out1), .out2(demultiplexer_1_out2),
    .out3(demultiplexer_1_out3), .out4(demultiplexer_1_out4), .out5(demultiplexer_1_out5),
    .out6(demultiplexer_1_out6), .out7(demultiplexer_1_out7), .out8(demultiplexer_1_out8),
    .out9(demultiplexer_1_out9), .out10(demultiplexer_1_out10), .out11(demultiplexer_1_out11),
    .out12(demultiplexer_1_out12), .out13(demultiplexer_1_out13), .out14(demultiplexer_1_out14),
    .out15(demultiplexer_1_out15), .out16(demultiplexer_1_out16), .out17(demultiplexer_1_out17),
    .out18(demultiplexer_1_out18), .out19(demultiplexer_1_out19), .out20(demultiplexer_1_out20),
    .out21(demultiplexer_1_out21), .out22(demultiplexer_1_out22), .out23(demultiplexer_1_out23), .in(1'b1),
    .sel(Row));  // open: out24, out25, out26, out27, out28, out29, out30, out31
  Register #(.width(16), .trigger("falling"), .Select("low")) register_1 (
    .D(DataIn), .en(demultiplexer_1_out0), .Q(out_6), .clk(WriteIn), .clr(Reset));
  Register #(.width(16), .trigger("falling"), .Select("low")) register_2 (
    .D(DataIn), .en(demultiplexer_1_out1), .Q(out_7), .clk(WriteIn), .clr(Reset));
  Register #(.width(16), .trigger("falling"), .Select("low")) register_3 (
    .D(DataIn), .en(demultiplexer_1_out2), .Q(out_8), .clk(WriteIn), .clr(Reset));
  Register #(.width(16), .trigger("falling"), .Select("low")) register_4 (
    .D(DataIn), .en(demultiplexer_1_out3), .Q(out_9), .clk(WriteIn), .clr(Reset));
  Register #(.width(16), .trigger("falling"), .Select("low")) register_5 (
    .D(DataIn), .en(demultiplexer_1_out4), .Q(out_10), .clk(WriteIn), .clr(Reset));
  Register #(.width(16), .trigger("falling"), .Select("low")) register_6 (
    .D(DataIn), .en(demultiplexer_1_out5), .Q(out_11), .clk(WriteIn), .clr(Reset));
  Register #(.width(16), .trigger("falling"), .Select("low")) register_7 (
    .D(DataIn), .en(demultiplexer_1_out6), .Q(out_12), .clk(WriteIn), .clr(Reset));
  Register #(.width(16), .trigger("falling"), .Select("low")) register_8 (
    .D(DataIn), .en(demultiplexer_1_out7), .Q(out_13), .clk(WriteIn), .clr(Reset));
  Register #(.width(16), .trigger("falling"), .Select("low")) register_9 (
    .D(DataIn), .en(demultiplexer_1_out8), .Q(out_14), .clk(WriteIn), .clr(Reset));
  Register #(.width(16), .trigger("falling"), .Select("low")) register_10 (
    .D(DataIn), .en(demultiplexer_1_out9), .Q(out_15), .clk(WriteIn), .clr(Reset));
  Register #(.width(16), .trigger("falling"), .Select("low")) register_11 (
    .D(DataIn), .en(demultiplexer_1_out10), .Q(out_16), .clk(WriteIn), .clr(Reset));
  Register #(.width(16), .trigger("falling"), .Select("low")) register_12 (
    .D(DataIn), .en(demultiplexer_1_out11), .Q(out_17), .clk(WriteIn), .clr(Reset));
  Register #(.width(16), .trigger("falling"), .Select("low")) register_13 (
    .D(DataIn), .en(demultiplexer_1_out12), .Q(out_18), .clk(WriteIn), .clr(Reset));
  Register #(.width(16), .trigger("falling"), .Select("low")) register_14 (
    .D(DataIn), .en(demultiplexer_1_out13), .Q(out_19), .clk(WriteIn), .clr(Reset));
  Register #(.width(16), .trigger("falling"), .Select("low")) register_15 (
    .D(DataIn), .en(demultiplexer_1_out14), .Q(out_20), .clk(WriteIn), .clr(Reset));
  Register #(.width(16), .trigger("falling"), .Select("low")) register_16 (
    .D(DataIn), .en(demultiplexer_1_out15), .Q(out_21), .clk(WriteIn), .clr(Reset));
  Register #(.width(16), .trigger("falling"), .Select("low")) register_17 (
    .D(DataIn), .en(demultiplexer_1_out16), .Q(out_22), .clk(WriteIn), .clr(Reset));
  Register #(.width(16), .trigger("falling"), .Select("low")) register_18 (
    .D(DataIn), .en(demultiplexer_1_out17), .Q(out_23), .clk(WriteIn), .clr(Reset));
  Register #(.width(16), .trigger("falling"), .Select("low")) register_19 (
    .D(DataIn), .en(demultiplexer_1_out18), .Q(out_24), .clk(WriteIn), .clr(Reset));
  Register #(.width(16), .trigger("falling"), .Select("low")) register_20 (
    .D(DataIn), .en(demultiplexer_1_out19), .Q(out_25), .clk(WriteIn), .clr(Reset));
  Register #(.width(16), .trigger("falling"), .Select("low")) register_21 (
    .D(DataIn), .en(demultiplexer_1_out20), .Q(out_26), .clk(WriteIn), .clr(Reset));
  Register #(.width(16), .trigger("falling"), .Select("low")) register_22 (
    .D(DataIn), .en(demultiplexer_1_out21), .Q(out_27), .clk(WriteIn), .clr(Reset));
  Register #(.width(16), .trigger("falling"), .Select("low")) register_23 (
    .D(DataIn), .en(demultiplexer_1_out22), .Q(out_28), .clk(WriteIn), .clr(Reset));
  Register #(.width(16), .trigger("falling"), .Select("low")) register_24 (
    .D(DataIn), .en(demultiplexer_1_out23), .Q(out_29), .clk(WriteIn), .clr(Reset));
  Multiplexer #(.select(5), .width(16), .enable("false")) multiplexer_1 (
    .in0(out_6), .in1(out_7), .in2(out_8), .in3(out_9), .in4(out_10), .in5(out_11), .in6(out_12),
    .in7(out_13), .in8(out_14), .in9(out_15), .in10(out_16), .in11(out_17), .in12(out_18), .in13(out_19),
    .in14(out_20), .in15(out_21), .in16(out_22), .in17(out_23), .in18(out_24), .in19(out_25), .in20(out_26),
    .in21(out_27), .in22(out_28), .in23(out_29), .in24(pull_resistor_1_node), .in25(pull_resistor_2_node),
    .in26(pull_resistor_3_node), .in27(pull_resistor_4_node), .in28(pull_resistor_5_node),
    .in29(pull_resistor_6_node), .in30(pull_resistor_7_node), .in31(pull_resistor_8_node), .out(DataOut),
    .sel(Row));
  Pull_Resistor pull_resistor_1 (.node(pull_resistor_1_node));
  Pull_Resistor pull_resistor_2 (.node(pull_resistor_2_node));
  Pull_Resistor pull_resistor_3 (.node(pull_resistor_3_node));
  Pull_Resistor pull_resistor_4 (.node(pull_resistor_4_node));
  Pull_Resistor pull_resistor_5 (.node(pull_resistor_5_node));
  Pull_Resistor pull_resistor_6 (.node(pull_resistor_6_node));
  Pull_Resistor pull_resistor_7 (.node(pull_resistor_7_node));
  Pull_Resistor pull_resistor_8 (.node(pull_resistor_8_node));

  // Other names for the same wires on the sheet: t1[15:0] = out_6; t2[15:0] = out_7; t3[15:0] = out_8;
  //   t4[15:0] = out_9; t5[15:0] = out_10; t6[15:0] = out_11; t7[15:0] = out_12; t8[15:0] = out_13; t9[15:0] = out_14;
  //   t10[15:0] = out_15; t11[15:0] = out_16; t12[15:0] = out_17; t13[15:0] = out_18; t14[15:0] = out_19;
  //   t15[15:0] = out_20; t16[15:0] = out_21; t17[15:0] = out_22; t18[15:0] = out_23; t19[15:0] = out_24;
  //   t20[15:0] = out_25; t21[15:0] = out_26; t22[15:0] = out_27; t23[15:0] = out_28; t24[15:0] = out_29
endmodule
