// Logisim project improved_port.circ as structural Verilog: 1 circuit, main circuit main
module main (
  input  PORTADDRWE,
  input  [15:0] PortA_In,
  input  PORTWE,
  input  PORTOE,
  input  [15:0] PortB_In,
  input  [15:0] DataBusIn,
  input  [15:0] PortC_In,
  input  [15:0] PortD_In,
  input  PORTRWWE,
  input  PORTEWE,
  input  Clock,
  input  Reset,
  output [15:0] DataBusOut,
  output [15:0] PortA_Out,
  output [15:0] PortB_Out,
  output [15:0] PortC_Out,
  output [15:0] PortD_Out
);

  wire and_1_out, and_2_out, demultiplexer_1_out0, demultiplexer_1_out1, demultiplexer_1_out2,
       demultiplexer_1_out3, multiplexer_1_out;
  wire [15:0] multiplexer_2_out, register_1_q, register_2_q, register_3_q, register_4_q, register_5_q,
       register_6_q, register_7_q;

  Register #(.width(16), .trigger("falling"), .Select("low")) register_1 (
    .D(DataBusIn), .en(PORTADDRWE), .Q(register_1_q), .clk(Clock), .clr(Reset));
  Register #(.width(16), .trigger("falling"), .Select("low")) register_2 (
    .D(DataBusIn), .en(PORTRWWE), .Q(register_2_q), .clk(Clock), .clr(Reset));
  Register #(.width(16), .trigger("falling"), .Select("low")) register_3 (
    .D(DataBusIn), .en(PORTEWE), .Q(register_3_q), .clk(Clock), .clr(Reset));
  Multiplexer #(.select(2), .enable("false")) multiplexer_1 (
    .in0(register_2_q[0]), .in1(register_2_q[1]), .in2(register_2_q[2]), .in3(register_2_q[3]),
    .out(multiplexer_1_out), .sel(register_1_q[1:0]));
  and and_1 (and_1_out, PORTOE, ~multiplexer_1_out);  // AND_Gate
  assign DataBusOut = and_1_out ? multiplexer_2_out : 16'bz;  // Controlled_Buffer controlled_buffer_1
  Demultiplexer #(.select(2), .enable("false")) demultiplexer_1 (
    .out0(demultiplexer_1_out0), .out1(demultiplexer_1_out1), .out2(demultiplexer_1_out2),
    .out3(demultiplexer_1_out3), .in(and_2_out), .sel(register_1_q[1:0]));
  and and_2 (and_2_out, PORTWE, multiplexer_1_out);
  Multiplexer #(.select(2), .width(16), .enable("false")) multiplexer_2 (
    .in0(PortA_In), .in1(PortB_In), .in2(PortC_In), .in3(PortD_In), .out(multiplexer_2_out),
    .sel(register_1_q[1:0]));
  Register #(.width(16), .trigger("falling"), .Select("low")) register_4 (
    .D(DataBusIn), .en(demultiplexer_1_out0), .Q(register_4_q), .clk(Clock), .clr(Reset));
  Register #(.width(16), .trigger("falling"), .Select("low")) register_5 (
    .D(DataBusIn), .en(demultiplexer_1_out1), .Q(register_5_q), .clk(Clock), .clr(Reset));
  Register #(.width(16), .trigger("falling"), .Select("low")) register_6 (
    .D(DataBusIn), .en(demultiplexer_1_out2), .Q(register_6_q), .clk(Clock), .clr(Reset));
  Register #(.width(16), .trigger("falling"), .Select("low")) register_7 (
    .D(DataBusIn), .en(demultiplexer_1_out3), .Q(register_7_q), .clk(Clock), .clr(Reset));
  assign PortA_Out = register_3_q[0] ? register_4_q : 16'bz;  // Controlled_Buffer controlled_buffer_2
  assign PortB_Out = register_3_q[1] ? register_5_q : 16'bz;  // Controlled_Buffer controlled_buffer_3
  assign PortC_Out = register_3_q[2] ? register_6_q : 16'bz;  // Controlled_Buffer controlled_buffer_4
  assign PortD_Out = register_3_q[3] ? register_7_q : 16'bz;  // Controlled_Buffer controlled_buffer_5
endmodule
