// Logisim project port_old.circ as structural Verilog: 1 circuit, main circuit main
module main (
  input  PORTADDRWE,
  input  [15:0] PortA_In,
  input  PORTWE,
  input  PORTOE,
  input  [15:0] PortB_In,
  input  [15:0] DataBusIn,
  input  [15:0] PortC_In,
  input  [15:0] PortD_In,
  input  Clock,
  input  Reset,
  input  PORTRWWE,
  output [15:0] DataBusOut,
  output [15:0] PortA_Out,
  output [15:0] PortB_Out,
  output [15:0] PortC_Out,
  output [15:0] PortD_Out
);

  wire and_1_out, and_2_out, multiplexer_1_out;
  wire [15:0] controlled_buffer_2_out, multiplexer_2_out, register_1_q, register_2_q;

  Register #(.width(16), .trigger("falling"), .Select("low")) register_1 (
    .D(DataBusIn), .en(PORTADDRWE), .Q(register_1_q), .clk(Clock), .clr(Reset));
  Register #(.width(16), .trigger("falling"), .Select("low")) register_2 (
    .D(DataBusIn), .en(PORTRWWE), .Q(register_2_q), .clk(Clock), .clr(Reset));
  Multiplexer #(.select(2), .enable("false")) multiplexer_1 (
    .in0(register_2_q[0]), .in1(register_2_q[1]), .in2(register_2_q[2]), .in3(register_2_q[3]),
    .out(multiplexer_1_out), .sel(register_1_q[1:0]));
  and and_1 (and_1_out, PORTOE, ~multiplexer_1_out);  // AND_Gate
  assign DataBusOut = and_1_out ? multiplexer_2_out : 16'bz;  // Controlled_Buffer controlled_buffer_1
  assign controlled_buffer_2_out = and_2_out ? DataBusIn : 16'bz;  // Controlled_Buffer controlled_buffer_2
  and and_2 (and_2_out, PORTWE, multiplexer_1_out);
  Multiplexer #(.select(2), .width(16), .enable("false")) multiplexer_2 (
    .in0(PortA_In), .in1(PortB_In), .in2(PortC_In), .in3(PortD_In), .out(multiplexer_2_out),
    .sel(register_1_q[1:0]));
  Demultiplexer #(.select(2), .width(16), .tristate("true"), .enable("false")) demultiplexer_1 (
    .out0(PortA_Out), .out1(PortB_Out), .out2(PortC_Out), .out3(PortD_Out), .in(controlled_buffer_2_out),
    .sel(register_1_q[1:0]));
endmodule
